// Logisim project rv32e_core_CS24B027.circ as structural Verilog: 12 circuits, main circuit SoC_sim_v2
module SoC_sim_v2 (
  input  RST,
  output uart_tx,
  output [31:0] gpio_out_en
);

  wire and_1_out, C, core_1_mem_wr, decoder_1_out0, decoder_1_out1, decoder_1_out2, decoder_1_out3;
  wire [1:0] core_1_addr;
  wire [2:0] core_1_strobe;
  wire [11:0] core_1_addr_2;
  wire [15:0] core_1_mem_wr_data, core_1_mem_wr_data_2, uart_v2_1_rd_data;
  wire [15:14] core_1_addr_3;
  wire [31:0] button_1_out, gpio_1_gpio_out, gpio_1_rd_data, main_memory_data_out, multiplexer_1_out;

  Clock clock_1 (.out(C));
  core core_1 (
    .mem_rd_data(multiplexer_1_out), .clk(C), .rst(RST), .mem_wr(core_1_mem_wr),
    .mem_wr_data({core_1_mem_wr_data_2, core_1_mem_wr_data}),
    .addr({core_1_addr_3, core_1_addr_2, core_1_addr}), .strobe(core_1_strobe));
  Decoder #(.enable("false"), .select(2)) decoder_1 (
    .out0(decoder_1_out0), .out1(decoder_1_out1), .out2(decoder_1_out2), .out3(decoder_1_out3),
    .sel(core_1_addr_3));
  and and_1 (and_1_out, core_1_mem_wr, decoder_1_out3);
  TTY tty_1 (.data(core_1_mem_wr_data[6:0]), .clk(C), .we(and_1_out), .clr(RST));
  memory main_memory (
    .data_in({core_1_mem_wr_data_2, core_1_mem_wr_data}), .addr({core_1_addr_2, core_1_addr}),
    .slave_en(decoder_1_out0), .wr_en(core_1_mem_wr), .strobe(core_1_strobe), .clk(C),
    .data_out(main_memory_data_out));
  uart_v2 uart_v2_1 (
    .clk(C), .rst(RST), .slave_en(decoder_1_out1), .addr(core_1_addr), .write_data(core_1_mem_wr_data),
    .write_en(core_1_mem_wr), .rd_data(uart_v2_1_rd_data), .tx(uart_tx));
  gpio gpio_1 (
    .clk(C), .rst(RST), .gpio_in(button_1_out), .slave_en(decoder_1_out2),
    .addr({core_1_addr_2[1:0], core_1_addr}), .write_data({core_1_mem_wr_data_2, core_1_mem_wr_data}),
    .write_en(core_1_mem_wr), .rd_data(gpio_1_rd_data), .gpio_out(gpio_1_gpio_out), .gpio_out_en(gpio_out_en));
  Multiplexer #(.select(2), .width(32)) multiplexer_1 (
    .in0(main_memory_data_out), .in1({{16{1'b0}}, uart_v2_1_rd_data}), .in2(gpio_1_rd_data),
    .in3({32{1'b0}}), .out(multiplexer_1_out), .sel(core_1_addr_3));
  // Probe on gpio_1_gpio_out[7:0]
  // Probe on gpio_1_gpio_out[15:8]
  DotMatrix #(.inputtype("row"), .matrixcols(8), .matrixrows(4)) dotmatrix_1 (
    .row0(gpio_1_gpio_out[7:0]), .row1(gpio_1_gpio_out[15:8]), .row2(gpio_1_gpio_out[23:16]),
    .row3(gpio_1_gpio_out[31:24]));
  Button button_1 (.out(button_1_out[0]));
  Button button_2 (.out(button_1_out[3]));
  Button button_3 (.out(button_1_out[1]));
  Button button_4 (.out(button_1_out[2]));

  // Other names for the same wires on the sheet: R = RST
endmodule

module core (
  input  [31:0] mem_rd_data,
  input  clk,
  input  rst,
  output mem_wr,
  output [31:0] mem_wr_data,
  output [15:0] addr,
  output [2:0] strobe
);

  wire branch, control_unit_1_addr_inst_or_data, control_unit_1_branch, control_unit_1_data_wb_or_load,
       control_unit_1_decode_exe, control_unit_1_decode_in, control_unit_1_fetch, control_unit_1_funct3_sel,
       control_unit_1_funct7_sel, control_unit_1_jal, control_unit_1_jalr, control_unit_1_mem,
       control_unit_1_opcode_a_sel, control_unit_1_pc_in_en, control_unit_1_rf_rd_in_en,
       control_unit_1_rs1_sel, control_unit_1_rs2_sel, control_unit_1_write_back;
  wire [1:0] control_unit_1_opcode_b_sel;
  wire [2:0] idecoder_1_funct3, idecoder_1_funct3_cntrl;
  wire [4:0] idecoder_1_rd, idecoder_1_rs1, idecoder_1_rs2;
  wire [5:0] idecoder_1_funct7;
  wire [5:5] idecoder_1_funct7_2;
  wire [8:0] idecoder_1_ins_type_decode;
  wire [15:0] alu_v1_1_alu_addr_out, alu_v1_1_alu_addr_out_2, rg_pc_q_2;
  wire [15:2] rg_pc_q;
  wire [31:0] adder_1_out, adder_2_out, adder_3_out, idecoder_1_b_or_j_imm, idecoder_1_i_type_imm,
       idecoder_1_s_type_imm, idecoder_1_u_type_imm, multiplexer_1_out, multiplexer_2_out, multiplexer_4_out,
       multiplexer_5_out, multiplexer_6_out, regfile16x32_1_rs1_val;

  Adder #(.width(32)) adder_1 (
    .a({rg_pc_q_2, rg_pc_q, 2'b00}), .b(idecoder_1_b_or_j_imm), .out(adder_1_out), .cin(1'b0));  // open: cout
  Adder #(.width(32)) adder_2 (
    .a({rg_pc_q_2, rg_pc_q, 2'b00}), .b(32'h4), .out(adder_2_out), .cin(1'b0));  // open: cout
  Multiplexer #(.width(32)) multiplexer_1 (.in0(adder_2_out), .in1(adder_1_out), .out(multiplexer_1_out), .sel(branch));
  // Probe on {rg_pc_q_2, rg_pc_q, 2'b00}
  // Probe on multiplexer_2_out
  Adder #(.width(32)) adder_3 (
    .a(regfile16x32_1_rs1_val), .b(idecoder_1_i_type_imm), .out(adder_3_out), .cin(1'b0));  // open: cout
  Multiplexer #(.width(32)) multiplexer_2 (
    .in0(multiplexer_1_out), .in1(adder_3_out), .out(multiplexer_2_out), .sel(control_unit_1_jalr));
  Register #(.width(30)) rg_pc (
    .D(multiplexer_2_out[31:2]), .en(control_unit_1_pc_in_en), .clk(clk), .Q({rg_pc_q_2, rg_pc_q}), .clr(rst));
  idecoder idecoder_1 (
    .instruction(mem_rd_data), .funct3_sel(control_unit_1_funct3_sel), .rs1_sel(control_unit_1_rs1_sel),
    .rs2_sel(control_unit_1_rs2_sel), .funct7_sel(control_unit_1_funct7_sel),
    .decode_en(control_unit_1_decode_in), .clk(clk), .rst(rst), .rd(idecoder_1_rd),
    .funct3(idecoder_1_funct3), .rs1(idecoder_1_rs1), .rs2(idecoder_1_rs2),
    .funct7({idecoder_1_funct7[5], idecoder_1_funct7_2[5], idecoder_1_funct7[4:0]}),
    .u_type_imm(idecoder_1_u_type_imm), .s_type_imm(idecoder_1_s_type_imm),
    .I_type_imm(idecoder_1_i_type_imm), .ins_type_decode(idecoder_1_ins_type_decode),
    .funct3_cntrl(idecoder_1_funct3_cntrl), .b_or_j_imm(idecoder_1_b_or_j_imm));
  control_unit control_unit_1 (
    .C(clk), .R(rst), .funct3(idecoder_1_funct3_cntrl), .inst_type_decode(idecoder_1_ins_type_decode),
    .pc_in_en(control_unit_1_pc_in_en), .addr_inst_or_data(control_unit_1_addr_inst_or_data),
    .funct3_sel(control_unit_1_funct3_sel), .rs1_sel(control_unit_1_rs1_sel),
    .rs2_sel(control_unit_1_rs2_sel), .funct7_sel(control_unit_1_funct7_sel),
    .opcode_a_sel(control_unit_1_opcode_a_sel), .opcode_b_sel(control_unit_1_opcode_b_sel),
    .mem_wr_en_cntrl(mem_wr), .rf_rd_in_en(control_unit_1_rf_rd_in_en),
    .data_wb_or_load(control_unit_1_data_wb_or_load), .mem_strobe(strobe),
    .decode_in(control_unit_1_decode_in), .fetch(control_unit_1_fetch),
    .decode_exe(control_unit_1_decode_exe), .mem(control_unit_1_mem), .write_back(control_unit_1_write_back),
    .branch(control_unit_1_branch), .jal(control_unit_1_jal), .jalr(control_unit_1_jalr));
  LED LED_3 (.in(control_unit_1_decode_exe));
  LED LED_4 (.in(control_unit_1_fetch));
  Multiplexer #(.width(16)) multiplexer_3 (
    .in0({rg_pc_q, 2'b00}), .in1(alu_v1_1_alu_addr_out), .out(addr), .sel(control_unit_1_addr_inst_or_data));
  LED LED_1 (.in(control_unit_1_write_back));
  LED LED_2 (.in(control_unit_1_mem));
  Multiplexer #(.width(32)) multiplexer_4 (
    .in0({alu_v1_1_alu_addr_out_2, alu_v1_1_alu_addr_out}), .in1(mem_rd_data), .out(multiplexer_4_out),
    .sel(control_unit_1_data_wb_or_load));
  regfile16x32 regfile16x32_1 (
    .rs2_sel(idecoder_1_rs2), .rs1_sel(idecoder_1_rs1), .rd_wr_sel(idecoder_1_rd),
    .rd_wr_en(control_unit_1_rf_rd_in_en), .rd_wr_val(multiplexer_4_out), .clk(clk), .rst(rst),
    .rs1_val(regfile16x32_1_rs1_val), .rs2_val(mem_wr_data));
  Multiplexer #(.width(32)) multiplexer_5 (
    .in0(regfile16x32_1_rs1_val), .in1({rg_pc_q_2, rg_pc_q, 2'b00}), .out(multiplexer_5_out),
    .sel(control_unit_1_opcode_a_sel));
  Multiplexer #(.select(2), .width(32)) multiplexer_6 (
    .in0(mem_wr_data), .in1(idecoder_1_u_type_imm), .in2(idecoder_1_s_type_imm), .in3(idecoder_1_i_type_imm),
    .out(multiplexer_6_out), .sel(control_unit_1_opcode_b_sel));
  alu_v1 alu_v1_1 (
    .a_input(multiplexer_5_out), .b_input(multiplexer_6_out), .func_7(idecoder_1_funct7_2[5]),
    .func_3(idecoder_1_funct3), .compare(control_unit_1_branch), .jal(control_unit_1_jal),
    .jalr(control_unit_1_jalr), .ALU_ADDR_OUT({alu_v1_1_alu_addr_out_2, alu_v1_1_alu_addr_out}),
    .take_branch(branch));

  // Other names for the same wires on the sheet: C = clk; R = rst
endmodule

// decoder
module idecoder (
  input  [31:0] instruction,
  input  funct3_sel,
  input  rs1_sel,
  input  rs2_sel,
  input  funct7_sel,
  input  decode_en,
  input  clk,
  input  rst,
  output [4:0] rd,
  output [2:0] funct3,
  output [4:0] rs1,
  output [4:0] rs2,
  output [6:0] funct7,
  output [31:0] u_type_imm,
  output [31:0] s_type_imm,
  output [31:0] I_type_imm,
  output [8:0] ins_type_decode,
  output [2:0] funct3_cntrl,
  output [31:0] b_or_j_imm
);

  wire [6:0] opcode;
  wire [31:0] bit_extender_3_out, bit_extender_4_out;

  Register #(.width(32)) rg_decode (
    .D(instruction), .en(decode_en), .clk(clk),
    .Q({u_type_imm[31], I_type_imm[10:0], u_type_imm[19:15], funct3_cntrl, rd, opcode}), .clr(rst));
  Multiplexer #(.width(3)) multiplexer_1 (.in0(funct3_cntrl), .in1(3'b000), .out(funct3), .sel(funct3_sel));
  Multiplexer #(.width(5)) multiplexer_2 (.in0(u_type_imm[19:15]), .in1({5{1'b0}}), .out(rs1), .sel(rs1_sel));
  Multiplexer #(.width(5)) multiplexer_3 (.in0({5{1'b0}}), .in1(I_type_imm[4:0]), .out(rs2), .sel(rs2_sel));
  Multiplexer #(.width(7)) multiplexer_4 (
    .in0({7{1'b0}}), .in1({u_type_imm[31], I_type_imm[10:5]}), .out(funct7), .sel(funct7_sel));
  assign I_type_imm[31:11] = {{20{u_type_imm[31]}}, u_type_imm[31]};  // Bit_Extender bit_extender_1
  Comparator #(.mode("unsigned"), .width(7)) comparator_1 (
    .a(opcode), .b(7'b0110111), .eq(ins_type_decode[0]));  // open: gt, lt
  Comparator #(.mode("unsigned"), .width(7)) comparator_2 (
    .a(opcode), .b(7'b0010111), .eq(ins_type_decode[1]));  // open: gt, lt
  Comparator #(.width(7)) comparator_3 (.a(opcode), .b(7'b1100011), .eq(ins_type_decode[2]));  // open: gt, lt
  Comparator #(.width(7)) comparator_4 (.a(opcode), .b(7'b1101111), .eq(ins_type_decode[3]));  // open: gt, lt
  Comparator #(.width(7)) comparator_5 (.a(opcode), .b(7'b1100111), .eq(ins_type_decode[4]));  // open: gt, lt
  Comparator #(.mode("unsigned"), .width(7)) comparator_6 (
    .a(opcode), .b(7'b0000011), .eq(ins_type_decode[5]));  // open: gt, lt
  Comparator #(.mode("unsigned"), .width(7)) comparator_7 (
    .a(opcode), .b(7'b0100011), .eq(ins_type_decode[6]));  // open: gt, lt
  Comparator #(.mode("unsigned"), .width(7)) comparator_8 (
    .a(opcode), .b(7'b0010011), .eq(ins_type_decode[7]));  // open: gt, lt
  Comparator #(.mode("unsigned"), .width(7)) comparator_9 (
    .a(opcode), .b(7'b0110011), .eq(ins_type_decode[8]));  // open: gt, lt
  assign u_type_imm[11:0] = {{11{1'b0}}, 1'b0};  // Bit_Extender bit_extender_2
  assign bit_extender_3_out = {{19{u_type_imm[31]}}, {u_type_imm[31], rd[0], I_type_imm[10:5], rd[4:1], 1'b0}};  // Bit_Extender bit_extender_3
  assign bit_extender_4_out = {{11{u_type_imm[31]}}, {u_type_imm[31], u_type_imm[19:15], funct3_cntrl, I_type_imm[0], I_type_imm[10:1], 1'b0}};  // Bit_Extender bit_extender_4
  Multiplexer #(.width(32)) multiplexer_5 (
    .in0(bit_extender_3_out), .in1(bit_extender_4_out), .out(b_or_j_imm), .sel(ins_type_decode[3]));
  // Probe on ins_type_decode

  assign s_type_imm = {I_type_imm[31:5], rd};
  assign {u_type_imm[30:20], u_type_imm[14:12]} = {I_type_imm[10:0], funct3_cntrl};

  // Other names for the same wires on the sheet: rd_4[3:0] = rd[4:1]; rd_1 = rd[0]; rs2_4[3:0] = I_type_imm[4:1];
  //   rs2_t[4:0] = I_type_imm[4:0]; f7[6:0] = {u_type_imm[31], I_type_imm[10:5]}; f7_6[5:0] = I_type_imm[10:5];
  //   rs2_1 = I_type_imm[0]; f3[2:0] = funct3_cntrl; rs1_t[4:0] = u_type_imm[19:15]; f7_1 = u_type_imm[31];
  //   j_or_branch = ins_type_decode[3]

  // Notes on the sheet:
  //   0-6 (7) opcode
  //   7 (1) rd / imm
  //   8-11 (4) rd / imm
  //   12-14 (3) funct3 / imm 
  //   15 -19 (5) rs1/ imm
  //   21-24 (4) rs2 / imm
  //   31 (1) funct7 / imm
  //   25-30 (6) funct7/ imm
  //   20 (1) rs2 / imm
  //   u_type_lui
  //   u_type_auipc
  //   i_type_load
  //   s_type_store
  //   i_type
  //   r_type
endmodule

// regfile16
module regfile16x32 (
  input  rd_wr_en,
  input  [31:0] rd_wr_val,
  input  [4:0] rd_wr_sel,
  input  [4:0] rs1_sel,
  input  [4:0] rs2_sel,
  input  clk,
  input  rst,
  output [31:0] rs1_val,
  output [31:0] rs2_val
);

  wire decoder_1_out0, decoder_1_out1, decoder_1_out2, decoder_1_out3, decoder_1_out4, decoder_1_out5,
       decoder_1_out6, decoder_1_out7, decoder_1_out8, decoder_1_out9, decoder_1_out10, decoder_1_out11,
       decoder_1_out12, decoder_1_out13, decoder_1_out14, decoder_1_out15;
  wire [31:0] x1_q, x2_q, x3_q, x4_q, x5_q, x6_q, x7_q, x8_q, x9_q, x10_q, x11_q, x12_q, x13_q, x14_q, x15_q;

  Decoder #(.select(4)) decoder_1 (
    .out0(decoder_1_out0), .out1(decoder_1_out1), .out2(decoder_1_out2), .out3(decoder_1_out3),
    .out4(decoder_1_out4), .out5(decoder_1_out5), .out6(decoder_1_out6), .out7(decoder_1_out7),
    .out8(decoder_1_out8), .out9(decoder_1_out9), .out10(decoder_1_out10), .out11(decoder_1_out11),
    .out12(decoder_1_out12), .out13(decoder_1_out13), .out14(decoder_1_out14), .out15(decoder_1_out15),
    .sel(rd_wr_sel[3:0]), .en(rd_wr_en));
  Register #(.width(32)) x8 (.D(rd_wr_val), .en(decoder_1_out8), .clk(clk), .Q(x8_q), .clr(rst));
  Register #(.width(32)) x1 (.D(rd_wr_val), .en(decoder_1_out1), .clk(clk), .Q(x1_q), .clr(rst));
  Register #(.width(32)) x9 (.D(rd_wr_val), .en(decoder_1_out9), .clk(clk), .Q(x9_q), .clr(rst));
  Register #(.width(32)) x2 (.D(rd_wr_val), .en(decoder_1_out2), .clk(clk), .Q(x2_q), .clr(rst));
  Register #(.width(32)) x10 (.D(rd_wr_val), .en(decoder_1_out10), .clk(clk), .Q(x10_q), .clr(rst));
  Register #(.width(32)) x3 (.D(rd_wr_val), .en(decoder_1_out3), .clk(clk), .Q(x3_q), .clr(rst));
  Register #(.width(32)) x11 (.D(rd_wr_val), .en(decoder_1_out11), .clk(clk), .Q(x11_q), .clr(rst));
  Register #(.width(32)) x4 (.D(rd_wr_val), .en(decoder_1_out4), .clk(clk), .Q(x4_q), .clr(rst));
  Register #(.width(32)) x12 (.D(rd_wr_val), .en(decoder_1_out12), .clk(clk), .Q(x12_q), .clr(rst));
  Register #(.width(32)) x5 (.D(rd_wr_val), .en(decoder_1_out5), .clk(clk), .Q(x5_q), .clr(rst));
  Register #(.width(32)) x13 (.D(rd_wr_val), .en(decoder_1_out13), .clk(clk), .Q(x13_q), .clr(rst));
  Register #(.width(32)) x6 (.D(rd_wr_val), .en(decoder_1_out6), .clk(clk), .Q(x6_q), .clr(rst));
  Register #(.width(32)) x14 (.D(rd_wr_val), .en(decoder_1_out14), .clk(clk), .Q(x14_q), .clr(rst));
  Register #(.width(32)) x7 (.D(rd_wr_val), .en(decoder_1_out7), .clk(clk), .Q(x7_q), .clr(rst));
  Register #(.width(32)) x15 (.D(rd_wr_val), .en(decoder_1_out15), .clk(clk), .Q(x15_q), .clr(rst));
  Multiplexer #(.select(4), .width(32)) multiplexer_1 (
    .in0({32{1'b0}}), .in1(x1_q), .in2(x2_q), .in3(x3_q), .in4(x4_q), .in5(x5_q), .in6(x6_q), .in7(x7_q),
    .in8(x8_q), .in9(x9_q), .in10(x10_q), .in11(x11_q), .in12(x12_q), .in13(x13_q), .in14(x14_q),
    .in15(x15_q), .out(rs1_val), .sel(rs1_sel[3:0]));
  Multiplexer #(.select(4), .width(32)) multiplexer_2 (
    .in0({32{1'b0}}), .in1(x1_q), .in2(x2_q), .in3(x3_q), .in4(x4_q), .in5(x5_q), .in6(x6_q), .in7(x7_q),
    .in8(x8_q), .in9(x9_q), .in10(x10_q), .in11(x11_q), .in12(x12_q), .in13(x13_q), .in14(x14_q),
    .in15(x15_q), .out(rs2_val), .sel(rs2_sel[3:0]));
endmodule

module alu_v1 (
  input  [31:0] a_input,
  input  [31:0] b_input,
  input  func_7,
  input  [2:0] func_3,
  input  compare,
  input  jal,
  input  jalr,
  output [31:0] ALU_ADDR_OUT,
  output take_branch
);

  wire and_2_out, comparator_1_eq, comparator_1_lt, comparator_2_lt, multiplexer_3_out, not_2_out, not_3_out,
       not_4_out, or_3_out;
  wire [0:0] comparator_3_lt, comparator_4_lt;
  wire [31:0] adder_1_out, adder_2_out, and_1_out, multiplexer_1_out, multiplexer_2_out, multiplexer_4_out,
       not_1_out, or_1_out, shifter_1_out, shifter_2_out, shifter_3_out, xor_1_out;

  // Probe on a_input
  // Probe on a_input
  // Probe on a_input
  Comparator #(.width(32)) comparator_1 (
    .a(a_input), .b(b_input), .eq(comparator_1_eq), .lt(comparator_1_lt));  // open: gt
  Comparator #(.mode("unsigned"), .width(32)) comparator_2 (
    .a(a_input), .b(b_input), .lt(comparator_2_lt));  // open: gt, eq
  Multiplexer #(.width(32)) multiplexer_1 (.in0(b_input), .in1(not_1_out), .out(multiplexer_1_out), .sel(func_7));
  assign not_1_out = ~b_input;  // NOT_Gate not_1, 32 bits wide
  Adder #(.width(32)) adder_1 (.a(a_input), .b(multiplexer_1_out), .out(adder_1_out), .cin(func_7));  // open: cout
  Shifter #(.width(32)) shifter_1 (.in(a_input), .\dist (b_input[4:0]), .out(shifter_1_out));
  Comparator #(.width(32)) comparator_3 (.a(a_input), .b(b_input), .lt(comparator_3_lt[0]));  // open: gt, eq
  Comparator #(.mode("unsigned"), .width(32)) comparator_4 (
    .a(a_input), .b(b_input), .lt(comparator_4_lt[0]));  // open: gt, eq
  assign xor_1_out = b_input ^ a_input;  // XOR_Gate xor_1, 32 bits wide
  Shifter #(.shift("lr"), .width(32)) shifter_2 (.in(a_input), .\dist (b_input[4:0]), .out(shifter_2_out));
  Multiplexer #(.width(32)) multiplexer_2 (
    .in0(shifter_2_out), .in1(shifter_3_out), .out(multiplexer_2_out), .sel(func_7));
  Shifter #(.shift("ar"), .width(32)) shifter_3 (.in(a_input), .\dist (b_input[4:0]), .out(shifter_3_out));
  assign or_1_out = a_input | b_input;  // OR_Gate or_1, 32 bits wide
  assign and_1_out = a_input & b_input;  // AND_Gate and_1, 32 bits wide
  not not_2 (not_2_out, comparator_1_eq);
  not not_3 (not_3_out, comparator_1_lt);
  not not_4 (not_4_out, comparator_2_lt);
  // Probe on b_input
  // Probe on b_input
  // Probe on b_input
  Multiplexer #(.select(3)) multiplexer_3 (
    .in0(comparator_1_eq), .in1(not_2_out), .in2(1'b0), .in3(1'b0), .in4(comparator_1_lt), .in5(not_3_out),
    .in6(comparator_2_lt), .in7(not_4_out), .out(multiplexer_3_out), .sel(func_3));
  // Probe on adder_1_out
  // Probe on adder_1_out
  and and_2 (and_2_out, multiplexer_3_out, compare);
  // Probe on adder_1_out
  Multiplexer #(.select(3), .width(32)) multiplexer_4 (
    .in0(adder_1_out), .in1(shifter_1_out), .in2({{31{1'b0}}, comparator_3_lt[0]}),
    .in3({{31{1'b0}}, comparator_4_lt[0]}), .in4(xor_1_out), .in5(multiplexer_2_out), .in6(or_1_out),
    .in7(and_1_out), .out(multiplexer_4_out), .sel(func_3));
  Adder #(.width(32)) adder_2 (.a(a_input), .b(32'h4), .out(adder_2_out), .cin(1'b0));  // open: cout
  or or_2 (take_branch, and_2_out, jal);
  Multiplexer #(.width(32)) multiplexer_5 (
    .in0(multiplexer_4_out), .in1(adder_2_out), .out(ALU_ADDR_OUT), .sel(or_3_out));
  or or_3 (or_3_out, jal, jalr);

  // Notes on the sheet:
  //   6). 110 --> OR
  //   7). 111 --> AND
  //   0). 000 --> ADD/SUB
  //   4). 100 --> XOR
  //   5). 101 --> SRL/SRA
  //   1). 001 --> SLL
  //   2). 010 --> SLT
  //   3). 011 --> SLTU, unsigned ADD/SUB
endmodule

module control_unit (
  input  C,
  input  R,
  input  [2:0] funct3,
  input  [8:0] inst_type_decode,
  output pc_in_en,
  output addr_inst_or_data,
  output funct3_sel,
  output rs1_sel,
  output rs2_sel,
  output funct7_sel,
  output opcode_a_sel,
  output [1:0] opcode_b_sel,
  output mem_wr_en_cntrl,
  output rf_rd_in_en,
  output data_wb_or_load,
  output [2:0] mem_strobe,
  output decode_in,
  output fetch,
  output decode_exe,
  output mem,
  output write_back,
  output branch,
  output jal,
  output jalr
);

  wire and_2_out, and_3_out, or_1_out, or_2_out, or_3_out, or_4_out, or_5_out, or_6_out, or_7_out, or_8_out,
       or_9_out, or_10_out, or_11_out, or_12_out;
  wire [1:0] adder_1_out, priority_encoder_2_out_addr, register_1_q;
  wire [2:0] and_15_out, and_16_out;
  wire [2:2] or_13_out, or_14_out;
  wire [8:0] and_1_out;
  wire [8:8] not_1_out;

  not not_1 (not_1_out[8], or_12_out);
  assign {and_1_out[8:5], jalr, jal, branch, and_1_out[1:0]} = {9{not_1_out[8]}} & inst_type_decode;  // AND_Gate and_1, 9 bits wide
  or or_1 (or_1_out, and_1_out[0], and_1_out[1], branch, jal, jalr, and_1_out[5], and_1_out[6], and_1_out[7], and_1_out[8]);
  or or_2 (or_2_out, and_1_out[6], and_1_out[5]);
  or or_3 (or_3_out, and_1_out[0], and_1_out[1]);
  or or_4 (or_4_out, and_1_out[1], jalr, jal);
  or or_5 (or_5_out, and_1_out[5], jalr, and_1_out[7]);
  priority_encoder priority_encoder_2 (
    .input0(and_1_out[8]), .input1(or_3_out), .input2(and_1_out[6]), .input3(or_5_out),
    .out_addr(priority_encoder_2_out_addr));  // open: valid
  or or_6 (or_6_out, jalr, and_1_out[0], and_1_out[1], and_1_out[5], and_1_out[7], and_1_out[8], jal);
  or or_7 (or_7_out, and_1_out[0], jal, and_1_out[1]);
  and and_2 (and_2_out, or_7_out, ~jalr, ~branch);  // AND_Gate
  or or_8 (or_8_out, and_1_out[6], branch, and_1_out[8]);
  and and_3 (and_3_out, ~funct3[1], funct3[0]);  // AND_Gate
  or or_9 (or_9_out, and_1_out[8], and_3_out);
  or or_10 (or_10_out, or_2_out, and_2_out);
  Adder #(.width(2)) adder_1 (.a(register_1_q), .b(2'b01), .out(adder_1_out), .cin(1'b0));  // open: cout
  or or_11 (or_11_out, or_12_out, write_back, mem);
  or or_12 (or_12_out, fetch, decode_exe);
  Register #(.width(2)) register_1 (.D(adder_1_out), .en(or_11_out), .clk(C), .Q(register_1_q), .clr(R));
  Decoder #(.enable("false"), .select(2)) decoder_1 (
    .out0(fetch), .out1(decode_exe), .out2(mem), .out3(write_back), .sel(register_1_q));
  or or_13 (or_13_out[2], write_back, mem);
  or or_14 (or_14_out[2], decode_exe, fetch);
  and and_4 (pc_in_en, write_back, or_1_out);
  and and_5 (addr_inst_or_data, or_13_out[2], or_2_out);
  and and_6 (funct3_sel, or_10_out, or_13_out[2]);
  and and_7 (rs1_sel, or_13_out[2], and_2_out);
  and and_8 (rs2_sel, or_13_out[2], or_8_out);
  and and_9 (funct7_sel, or_13_out[2], or_9_out);
  and and_10 (opcode_a_sel, or_13_out[2], or_4_out);
  assign opcode_b_sel = {2{or_13_out[2]}} & priority_encoder_2_out_addr;  // AND_Gate and_11, 2 bits wide
  and and_12 (mem_wr_en_cntrl, write_back, and_1_out[6]);
  and and_13 (rf_rd_in_en, write_back, or_6_out);
  and and_14 (data_wb_or_load, write_back, and_1_out[5]);
  assign and_15_out = {3{or_13_out[2]}} & funct3;  // AND_Gate and_15, 3 bits wide
  assign and_16_out = {3{or_14_out[2]}} & 3'b010;  // AND_Gate and_16, 3 bits wide
  assign mem_strobe = and_15_out | and_16_out;  // OR_Gate or_15, 3 bits wide

  assign decode_in = decode_exe;

  // Notes on the sheet:
  //   u_type_lui
  //   u_type_auipc
  //   i_type
  //   r_type
  //   branch
  //   i_type_load
  //   s_type_store
  //   jal
  //   jalr
  //   sending pc to alu for jal & jalr
  //   opcode_b_sel change for jalr
  //   write_to_reg_sel
  //   logic for rs1_sel
  //   control_micro_ops_state
  //   fetch
  //   decode/exe
  //   mem
  //   writeback
endmodule

module priority_encoder (
  input  input0,
  input  input1,
  input  input2,
  input  input3,
  output [1:0] out_addr,
  output valid
);

  wire and_1_out, not_1_out;

  not not_1 (not_1_out, input2);
  or or_1 (out_addr[1], input3, input2);
  and and_1 (and_1_out, not_1_out, input1);
  or or_2 (valid, out_addr[1], input2, input0);
  or or_3 (out_addr[0], input3, and_1_out);
endmodule

module uart_v2 (
  input  clk,
  input  rst,
  input  slave_en,
  input  [1:0] addr,
  input  [15:0] write_data,
  input  write_en,
  output [15:0] rd_data,
  output tx
);

  wire and_1_out, and_2_out, and_3_out, and_4_out, and_5_out, and_6_out, and_7_out, and_8_out, and_9_out,
       and_10_out, comparator_1_eq, decoder_1_out0, decoder_1_out2, multiplexer_3_out, multiplexer_5_out,
       nor_1_out, not_1_out, or_1_out, or_2_out, or_3_out, or_4_out, register_1_q, register_2_q, xor_1_out;
  wire [0:0] write_busy_q;
  wire [3:0] adder_2_out, multiplexer_4_out, tx_state_reg_q;
  wire [7:0] multiplexer_2_out, tx_data_reg_q;
  wire [15:0] baud_reg_q;
  wire [19:0] adder_1_out, baud_counter_q, multiplexer_1_out;

  and and_1 (and_1_out, slave_en, write_en);
  Decoder #(.enable("false"), .select(2)) decoder_1 (
    .out0(decoder_1_out0), .out2(decoder_1_out2), .sel(addr));  // open: out1, out3
  and and_2 (and_2_out, decoder_1_out2, and_1_out);
  Register #(.width(1)) write_busy (.D(and_3_out), .en(or_1_out), .clk(clk), .Q(write_busy_q[0]), .clr(rst));
  and and_3 (and_3_out, and_2_out, ~and_10_out);  // AND_Gate
  or or_1 (or_1_out, and_2_out, and_10_out);
  Adder #(.width(20)) adder_1 (.a(baud_counter_q), .b(20'h1), .out(adder_1_out), .cin(1'b0));  // open: cout
  and and_4 (and_4_out, decoder_1_out0, and_1_out);
  Multiplexer #(.width(20)) multiplexer_1 (
    .in0(adder_1_out), .in1({20{1'b0}}), .out(multiplexer_1_out), .sel(or_2_out));
  or or_2 (or_2_out, and_10_out, comparator_1_eq);
  Multiplexer #(.width(8)) multiplexer_2 (
    .in0({1'b0, tx_data_reg_q[7:1]}), .in1(write_data[7:0]), .out(multiplexer_2_out), .sel(and_2_out));
  Register #(.width(20)) baud_counter (.D(multiplexer_1_out), .en(or_3_out), .clk(clk), .Q(baud_counter_q), .clr(rst));
  or or_3 (or_3_out, write_busy_q[0], and_10_out, comparator_1_eq);
  Register #(.width(16)) baud_reg (.D(write_data), .en(and_4_out), .clk(clk), .Q(baud_reg_q), .clr(rst));
  and and_5 (and_5_out, xor_1_out, ~and_8_out);  // AND_Gate
  and and_6 (and_6_out, xor_1_out, write_busy_q[0]);
  Multiplexer multiplexer_3 (.in0(and_5_out), .in1(and_2_out), .out(multiplexer_3_out), .sel(and_7_out));
  or or_4 (or_4_out, and_6_out, and_10_out);
  Register tx_data_reg (.D(multiplexer_2_out), .en(multiplexer_3_out), .clk(clk), .Q(tx_data_reg_q), .clr(rst));
  Adder #(.width(4)) adder_2 (.a(tx_state_reg_q), .b(4'b0001), .out(adder_2_out), .cin(1'b0));  // open: cout
  Multiplexer #(.width(4)) multiplexer_4 (.in0(adder_2_out), .in1(4'b0000), .out(multiplexer_4_out), .sel(and_10_out));
  Comparator #(.mode("unsigned"), .width(20)) comparator_1 (
    .a(baud_counter_q), .b({baud_reg_q, 4'b0000}), .eq(comparator_1_eq));  // open: gt, lt
  Register #(.width(4)) tx_state_reg (.D(multiplexer_4_out), .en(or_4_out), .clk(clk), .Q(tx_state_reg_q), .clr(rst));
  Register #(.width(1)) register_1 (.D(not_1_out), .en(comparator_1_eq), .clk(clk), .Q(register_1_q), .clr(rst));
  Multiplexer multiplexer_5 (.in0(1'b1), .in1(1'b0), .out(multiplexer_5_out), .sel(and_8_out));
  Multiplexer multiplexer_6 (.in0(multiplexer_5_out), .in1(tx_data_reg_q[0]), .out(tx), .sel(nor_1_out));
  not not_1 (not_1_out, register_1_q);
  Register #(.width(1)) register_2 (.D(not_1_out), .en(write_busy_q[0]), .clk(clk), .Q(register_2_q), .clr(rst));
  nor nor_1 (nor_1_out, and_7_out, and_8_out, and_9_out, and_10_out);
  and and_7 (and_7_out, ~tx_state_reg_q[0], ~tx_state_reg_q[1], ~tx_state_reg_q[2], ~tx_state_reg_q[3]);  // AND_Gate
  and and_8 (and_8_out, tx_state_reg_q[0], ~tx_state_reg_q[1], ~tx_state_reg_q[2], ~tx_state_reg_q[3]);  // AND_Gate
  and and_9 (and_9_out, ~tx_state_reg_q[0], tx_state_reg_q[1], ~tx_state_reg_q[2], tx_state_reg_q[3]);  // AND_Gate
  and and_10 (and_10_out, tx_state_reg_q[0], tx_state_reg_q[1], ~tx_state_reg_q[2], tx_state_reg_q[3]);  // AND_Gate
  xor xor_1 (xor_1_out, not_1_out, register_2_q);
  Multiplexer #(.select(2), .width(16)) multiplexer_7 (
    .in0(baud_reg_q), .in1({16{1'b0}}), .in2({16{1'b0}}), .in3({{15{1'b0}}, write_busy_q[0]}), .out(rd_data),
    .sel(addr));

  // Other names for the same wires on the sheet: c = clk; r = rst
endmodule

module gpio (
  input  clk,
  input  rst,
  input  [31:0] gpio_in,
  input  slave_en,
  input  [3:0] addr,
  input  [31:0] write_data,
  input  write_en,
  output [31:0] rd_data,
  output [31:0] gpio_out,
  output [31:0] gpio_out_en
);

  wire and_1_out, and_2_out, and_3_out, and_4_out, and_5_out, and_6_out, comparator_1_eq, register_1_q;
  wire [0:0] not_1_out;
  wire [31:0] adder_1_out, counter_q, multiplexer_1_out, reg_data_in_q;

  and and_1 (and_1_out, ~addr[0], ~addr[1], ~addr[2], ~addr[3]);  // AND_Gate
  and and_2 (and_2_out, ~addr[0], ~addr[1], addr[2], ~addr[3]);  // AND_Gate
  and and_3 (and_3_out, slave_en, write_en);
  and and_4 (and_4_out, slave_en, write_en);
  Adder #(.width(32)) adder_1 (.a(counter_q), .b(32'h1), .out(adder_1_out), .cin(1'b0));  // open: cout
  and and_5 (and_5_out, and_4_out, and_1_out);
  and and_6 (and_6_out, and_3_out, and_2_out);
  Multiplexer #(.width(32)) multiplexer_1 (
    .in0(adder_1_out), .in1({32{1'b0}}), .out(multiplexer_1_out), .sel(comparator_1_eq));
  Register #(.width(32)) counter (.D(multiplexer_1_out), .en(1'b1), .clk(clk), .Q(counter_q), .clr(rst));
  Register #(.width(32)) reg_direction (.D(write_data), .en(and_5_out), .clk(clk), .Q(gpio_out_en), .clr(rst));
  Register #(.width(32)) reg_data_out (.D(write_data), .en(and_6_out), .clk(clk), .Q(gpio_out), .clr(rst));
  Register #(.width(32)) reg_data_in (.D(gpio_in), .en(1'b1), .clk(clk), .Q(reg_data_in_q), .clr(rst));
  Comparator #(.mode("unsigned"), .width(32)) comparator_1 (
    .a(counter_q), .b(32'h17d7840), .eq(comparator_1_eq));  // open: gt, lt
  Register #(.width(1)) register_1 (.D(not_1_out[0]), .en(comparator_1_eq), .clk(clk), .Q(register_1_q), .clr(rst));
  not not_1 (not_1_out[0], register_1_q);
  Multiplexer #(.select(2), .width(32)) multiplexer_2 (
    .in0({32{1'b0}}), .in1({32{1'b0}}), .in2(reg_data_in_q), .in3({32{1'b0}}), .out(rd_data), .sel(addr[3:2]));

  // Other names for the same wires on the sheet: c = clk; r = rst
endmodule

module memory (
  input  [31:0] data_in,
  input  [13:0] addr,
  input  slave_en,
  input  wr_en,
  input  [2:0] strobe,
  input  clk,
  output [31:0] data_out
);

  wire and_1_out, and_2_out, and_3_out, and_4_out, and_5_out;
  wire [1:1] decoder_2_out0, decoder_2_out1;
  wire [3:0] decoder_1_out0, multiplexer_1_out;
  wire [7:0] multiplexer_3_out;
  wire [15:0] bank0_dout, bank2_dout, multiplexer_2_out;
  wire [31:0] shifter_1_out, zero_sign_extend_8_1_outp, zero_sign_extend_16_1_outp;

  Shifter #(.width(32)) shifter_1 (.in(data_in), .\dist ({addr[1:0], 3'b000}), .out(shifter_1_out));
  and and_1 (and_1_out, slave_en, wr_en);
  RAM #(.addrWidth(12), .asyncread("true")) bank3 (
    .addr(addr[13:2]), .we(and_2_out), .oe(1'b1), .clk(clk), .din(shifter_1_out[31:24]),
    .dout(bank2_dout[15:8]));
  Decoder #(.enable("false"), .select(2)) decoder_1 (
    .out0(decoder_1_out0[0]), .out1(decoder_1_out0[1]), .out2(decoder_1_out0[2]), .out3(decoder_1_out0[3]),
    .sel(addr[1:0]));
  Decoder #(.enable("false")) decoder_2 (.out0(decoder_2_out0[1]), .out1(decoder_2_out1[1]), .sel(addr[1]));
  and and_2 (and_2_out, and_1_out, multiplexer_1_out[3]);
  Multiplexer #(.select(2), .width(4)) multiplexer_1 (
    .in0(decoder_1_out0), .in1({{2{decoder_2_out1[1]}}, {2{decoder_2_out0[1]}}}), .in2(4'b1111),
    .in3(4'b0000), .out(multiplexer_1_out), .sel(strobe[1:0]));
  RAM #(.addrWidth(12), .asyncread("true")) bank2 (
    .addr(addr[13:2]), .we(and_3_out), .oe(1'b1), .clk(clk), .din(shifter_1_out[23:16]),
    .dout(bank2_dout[7:0]));
  and and_3 (and_3_out, and_1_out, multiplexer_1_out[2]);
  Multiplexer #(.width(16)) multiplexer_2 (.in0(bank0_dout), .in1(bank2_dout), .out(multiplexer_2_out), .sel(addr[1]));
  Multiplexer #(.select(2), .width(8)) multiplexer_3 (
    .in0(bank0_dout[7:0]), .in1(bank0_dout[15:8]), .in2(bank2_dout[7:0]), .in3(bank2_dout[15:8]),
    .out(multiplexer_3_out), .sel(addr[1:0]));
  RAM #(.addrWidth(12), .asyncread("true")) bank1 (
    .addr(addr[13:2]), .we(and_4_out), .oe(1'b1), .clk(clk), .din(shifter_1_out[15:8]),
    .dout(bank0_dout[15:8]));
  and and_4 (and_4_out, and_1_out, multiplexer_1_out[1]);
  zero_sign_extend_16 zero_sign_extend_16_1 (
    .inpt(multiplexer_2_out), .sign_ext_en(strobe[2]), .outp(zero_sign_extend_16_1_outp));
  zero_sign_extend_8 zero_sign_extend_8_1 (
    .inpt(multiplexer_3_out), .sign_ext_en(strobe[2]), .outp(zero_sign_extend_8_1_outp));
  Multiplexer #(.select(2), .width(32)) multiplexer_4 (
    .in0(zero_sign_extend_8_1_outp), .in1(zero_sign_extend_16_1_outp), .in2({bank2_dout, bank0_dout}),
    .in3({32{1'b0}}), .out(data_out), .sel(strobe[1:0]));
  // Probe on data_out
  RAM #(.addrWidth(12), .asyncread("true")) bank0 (
    .addr(addr[13:2]), .we(and_5_out), .oe(1'b1), .clk(clk), .din(shifter_1_out[7:0]), .dout(bank0_dout[7:0]));
  and and_5 (and_5_out, and_1_out, multiplexer_1_out[0]);
endmodule

module zero_sign_extend_8 (
  input  [7:0] inpt,
  input  sign_ext_en,
  output [31:0] outp
);

  and and_1 (outp[31], inpt[7], sign_ext_en);

  assign outp[30:0] = {{24{outp[31]}}, inpt[6:0]};
endmodule

module zero_sign_extend_16 (
  input  [15:0] inpt,
  input  sign_ext_en,
  output [31:0] outp
);

  and and_1 (outp[31], inpt[15], sign_ext_en);

  assign outp[30:0] = {{16{outp[31]}}, inpt[14:0]};
endmodule
