// Logisim project RV32IM-2_stage_pipeline_BP64.circ as structural Verilog: 15 circuits, main circuit core_v2
module core_v2 (
  input  clk,
  input  in_2,
  input  rst
);

  wire and_1_out, and_2_out, and_3_out, and_4_out, and_5_out, and_6_out, and_7_out, and_8_out, C,
       clock_1_out, comparator_1_eq, not_1_out, or_1_out, or_2_out, s1_s2_pipe_1_s2_ready_stall,
       stage1_1_ready_stall, stage2_1_branch, stage2_1_mem_wr_en, stage2_1_rd_en, stage2_1_s2_br,
       stage2_1_s2_load;
  wire [1:0] bp_64_1_msb0, bp_64_1_msb1;
  wire [2:0] stage2_1_strobe;
  wire [4:0] stage2_1_s2_rd_sel;
  wire [18:0] s1_s2_pipe_1_s2_inst_meta_data, stage1_1_inst_meta_data;
  wire [31:0] adder_1_out, adder_2_out, adder_4_out, memory_1_data_out, ram_1_dout, register_1_q,
       register_2_q, register_4_q, register_5_q, s1_s2_pipe_1_s2_br_imm, s1_s2_pipe_1_s2_imm_val,
       s1_s2_pipe_1_s2_pc, s1_s2_pipe_1_s2_rs1_val, s1_s2_pipe_1_s2_rs2_val, stage1_1_br_imm,
       stage1_1_imm_stage_2, stage1_1_pc, stage1_1_rs1_val, stage1_1_rs2_val, stage2_1_addr, stage2_1_rd_val,
       stage2_1_st_data;
  wire [63:0] adder_3_out, register_3_q;

  Register #(.width(32)) register_1 (
    .D(adder_2_out), .en(s1_s2_pipe_1_s2_ready_stall), .clk(C), .Q(register_1_q), .clr(rst));
  Clock clock_1 (.out(clock_1_out));
  assign C = or_1_out ? clock_1_out : 1'bz;  // Controlled_Buffer controlled_buffer_1
  Adder #(.width(32)) adder_1 (.a(register_2_q), .b(32'h1), .out(adder_1_out));  // open: cin, cout
  Adder #(.width(32)) adder_2 (.a(register_1_q), .b(32'h1), .out(adder_2_out));  // open: cin, cout
  Register #(.width(32)) register_2 (.D(adder_1_out), .en(and_1_out), .clk(C), .Q(register_2_q), .clr(rst));
  or or_1 (or_1_out, not_1_out, in_2);
  Adder #(.width(64)) adder_3 (.a(register_3_q), .b(64'h1), .out(adder_3_out), .cin(1'b0));  // open: cout
  and and_1 (and_1_out, stage2_1_s2_br, or_2_out);
  or or_2 (or_2_out, and_5_out, and_6_out);
  not not_1 (not_1_out, comparator_1_eq);
  Comparator #(.width(32)) comparator_1 (.a(stage1_1_pc), .b(32'h2d8), .eq(comparator_1_eq));  // open: gt, lt
  and and_2 (and_2_out, stage2_1_s2_br, ~and_6_out, ~and_5_out);  // AND_Gate
  Register #(.width(64)) register_3 (.D(adder_3_out), .en(1'b1), .clk(C), .Q(register_3_q), .clr(rst));
  Register #(.width(32)) register_4 (.D(adder_4_out), .en(and_2_out), .clk(C), .Q(register_4_q), .clr(rst));
  Adder #(.width(32)) adder_4 (.a(register_4_q), .b(32'h1), .out(adder_4_out));  // open: cin, cout
  // Probe on stage1_1_pc
  // Probe on s1_s2_pipe_1_s2_pc
  RAM #(.addrWidth(12), .asyncread("true"), .dataWidth(32)) ram_1 (
    .addr(stage1_1_pc[13:2]), .we(1'b0), .oe(1'b1), .clk(C), .din({32{1'b0}}), .dout(ram_1_dout));
  stage1 stage1_1 (
    .s2_br_inst(stage2_1_s2_br), .s2_rd_en(stage2_1_rd_en), .s2_rd_val(stage2_1_rd_val),
    .s2_rd_sel(stage2_1_s2_rd_sel), .branch_out(stage2_1_branch), .instruction(ram_1_dout),
    .s2_br_imm(s1_s2_pipe_1_s2_br_imm), .s2_load(stage2_1_s2_load), .bp_out(bp_64_1_msb0[1]),
    .b_taken_err(and_5_out), .b_nt_err(and_6_out), .clk(C), .rst(rst), .pc(stage1_1_pc),
    .rs1_val(stage1_1_rs1_val), .rs2_val(stage1_1_rs2_val), .inst_meta_data(stage1_1_inst_meta_data),
    .imm_stage_2(stage1_1_imm_stage_2), .ready_stall(stage1_1_ready_stall), .br_imm(stage1_1_br_imm));
  and and_3 (and_3_out, stage2_1_s2_br, stage2_1_branch);
  s1_s2_pipe s1_s2_pipe_1 (
    .s1_pc(stage1_1_pc), .s1_rs1_val(stage1_1_rs1_val), .s1_rs2_val(stage1_1_rs2_val),
    .s1_inst_meta_data(stage1_1_inst_meta_data), .s1_imm_val(stage1_1_imm_stage_2),
    .s1_ready_stall(stage1_1_ready_stall), .s1_br_imm(stage1_1_br_imm), .clk(C), .rst(rst),
    .s2_pc(s1_s2_pipe_1_s2_pc), .s2_rs1_val(s1_s2_pipe_1_s2_rs1_val), .s2_rs2_val(s1_s2_pipe_1_s2_rs2_val),
    .s2_inst_meta_data(s1_s2_pipe_1_s2_inst_meta_data), .s2_imm_val(s1_s2_pipe_1_s2_imm_val),
    .s2_ready_stall(s1_s2_pipe_1_s2_ready_stall), .s2_br_imm(s1_s2_pipe_1_s2_br_imm));
  // Probe on stage2_1_st_data
  // Probe on stage2_1_st_data
  // Probe on memory_1_data_out
  // Probe on memory_1_data_out
  bp_64 bp_64_1 (
    .wr_en(stage2_1_s2_br), .pc_write(s1_s2_pipe_1_s2_pc), .inc(and_3_out), .pc_read0(stage1_1_pc), .clk(C),
    .rst(rst), .pc_read1(s1_s2_pipe_1_s2_pc), .msb0(bp_64_1_msb0), .msb1(bp_64_1_msb1));
  and and_4 (and_4_out, bp_64_1_msb1[1], stage2_1_s2_br);
  stage2 stage2_1 (
    .ld_data(memory_1_data_out), .s2_pc(s1_s2_pipe_1_s2_pc), .s2_rs1_val(s1_s2_pipe_1_s2_rs1_val),
    .s2_rs2_val(s1_s2_pipe_1_s2_rs2_val), .s2_inst_meta_data(s1_s2_pipe_1_s2_inst_meta_data),
    .s2_imm_val(s1_s2_pipe_1_s2_imm_val), .s2_ready_stall(s1_s2_pipe_1_s2_ready_stall),
    .s2_rd_sel(stage2_1_s2_rd_sel), .rd_en(stage2_1_rd_en), .rd_val(stage2_1_rd_val),
    .branch(stage2_1_branch), .addr(stage2_1_addr), .mem_wr_en(stage2_1_mem_wr_en), .strobe(stage2_1_strobe),
    .st_data(stage2_1_st_data), .s2_br(stage2_1_s2_br), .s2_load(stage2_1_s2_load));
  and and_5 (and_5_out, ~and_3_out, stage2_1_s2_br, and_4_out);  // AND_Gate
  and and_6 (and_6_out, and_3_out, stage2_1_s2_br, ~and_4_out);  // AND_Gate
  // Probe on stage2_1_addr
  // Probe on stage2_1_addr
  and and_7 (and_7_out, stage2_1_addr[14], ~stage2_1_addr[15]);  // AND_Gate
  memory memory_1 (
    .data_in(stage2_1_st_data), .addr(stage2_1_addr[13:0]), .slave_en(and_7_out), .wr_en(stage2_1_mem_wr_en),
    .strobe(stage2_1_strobe), .clk(C), .data_out(memory_1_data_out));
  and and_8 (and_8_out, stage2_1_addr[14], stage2_1_addr[15], stage2_1_mem_wr_en);
  TTY #(.cols(120), .rows(48)) tty_1 (.data(stage2_1_st_data[6:0]), .clk(C), .we(and_8_out), .clr(rst));
  Register #(.width(32)) register_5 (.D(stage2_1_st_data), .en(and_8_out), .clk(C), .Q(register_5_q), .clr(rst));
  // Probe on register_5_q

  // Other names for the same wires on the sheet: R = rst

  // Notes on the sheet:
  //   branch_ins_count
  //   branch_misses
  //   cycles
  //   branch_hits
  //   s1_read
  //   s2_read and write
  //   branch taken misprediction
  //   branch not taken misprediction
endmodule

module stage1 (
  input  s2_br_inst,
  input  s2_rd_en,
  input  [31:0] s2_rd_val,
  input  [4:0] s2_rd_sel,
  input  branch_out,
  input  [31:0] instruction,
  input  [31:0] s2_br_imm,
  input  s2_load,
  input  bp_out,
  input  b_taken_err,
  input  b_nt_err,
  input  clk,
  input  rst,
  output [31:0] pc,
  output [31:0] rs1_val,
  output [31:0] rs2_val,
  output [18:0] inst_meta_data,
  output [31:0] imm_stage_2,
  output ready_stall,
  output [31:0] br_imm
);

  wire adder_1_cout, and_1_out, and_2_out, comparator_1_eq, comparator_2_eq, comparator_3_eq,
       comparator_4_eq, idecoder_1_pc_sel_mux_a, idecoder_1_ready_stall, not_1_out, not_2_out, or_1_out;
  wire [1:0] idecoder_1_pc_sel_mux_b;
  wire [4:0] idecoder_1_rs1, idecoder_1_rs2;
  wire [31:0] adder_2_out, idecoder_1_i_type_imm, idecoder_1_j_type_imm, multiplexer_1_out,
       multiplexer_2_out, multiplexer_3_out, pc_minus_br_plus_4, pc_plus_br_minus_4, regfile32x32_1_rs1_val,
       regfile32x32_1_rs2_val, subtractor_1_out;

  Subtractor #(.width(32)) subtractor_1 (.a(s2_br_imm), .b(32'h4), .out(subtractor_1_out));  // open: bin, bout
  Adder #(.width(32)) adder_1 (
    .a({pc[31:2], 2'b00}), .b(subtractor_1_out), .out(pc_plus_br_minus_4), .cout(adder_1_cout));  // open: cin
  Subtractor #(.width(32)) subtractor_2 (
    .a({pc[31:2], 2'b00}), .b(subtractor_1_out), .out(pc_minus_br_plus_4), .bin(adder_1_cout));  // open: bout
  Multiplexer #(.select(2), .width(32)) multiplexer_1 (
    .in0(32'h4), .in1(idecoder_1_j_type_imm), .in2(idecoder_1_i_type_imm), .in3(br_imm),
    .out(multiplexer_1_out), .sel(idecoder_1_pc_sel_mux_b));
  Multiplexer #(.width(32)) multiplexer_2 (
    .in0({pc[31:2], 2'b00}), .in1(rs1_val), .out(multiplexer_2_out), .sel(idecoder_1_pc_sel_mux_a));
  Adder #(.width(32)) adder_2 (
    .a(multiplexer_2_out), .b(multiplexer_1_out), .out(adder_2_out), .cin(1'b0));  // open: cout
  // Probe on adder_2_out
  Multiplexer #(.select(2), .width(32)) multiplexer_3 (
    .in0(adder_2_out), .in1(pc_minus_br_plus_4), .in2(pc_plus_br_minus_4), .out(multiplexer_3_out),
    .sel({b_nt_err, b_taken_err}));  // open: in3
  // Probe on {pc[31:2], 2'b00}
  Register #(.width(30)) rg_pc (
    .D(multiplexer_3_out[31:2]), .en(idecoder_1_ready_stall), .clk(clk), .Q(pc[31:2]), .clr(rst));
  idecoder idecoder_1 (
    .instruction(instruction), .bp_out(bp_out), .rd(inst_meta_data[8:4]), .funct_3(inst_meta_data[11:9]),
    .rs1(idecoder_1_rs1), .rs2(idecoder_1_rs2), .funct_7(inst_meta_data[18:12]), .imm_stage_2(imm_stage_2),
    .j_type_imm(idecoder_1_j_type_imm), .b_type_imm(br_imm), .I_type_imm(idecoder_1_i_type_imm),
    .ins_encoding_stage2(inst_meta_data[3:0]), .pc_sel_mux_a(idecoder_1_pc_sel_mux_a),
    .pc_sel_mux_b(idecoder_1_pc_sel_mux_b), .ready_stall(idecoder_1_ready_stall));
  Comparator #(.width(5)) comparator_1 (.a(idecoder_1_rs1), .b({5{1'b0}}), .eq(comparator_1_eq));  // open: gt, lt
  not not_1 (not_1_out, comparator_1_eq);
  Comparator #(.width(5)) comparator_2 (.a({5{1'b0}}), .b(idecoder_1_rs2), .eq(comparator_2_eq));  // open: gt, lt
  Comparator #(.width(5)) comparator_3 (.a(idecoder_1_rs1), .b(s2_rd_sel), .eq(comparator_3_eq));  // open: gt, lt
  Comparator #(.width(5)) comparator_4 (.a(idecoder_1_rs2), .b(s2_rd_sel), .eq(comparator_4_eq));  // open: gt, lt
  not not_2 (not_2_out, comparator_2_eq);
  or or_1 (or_1_out, b_taken_err, b_nt_err);
  and and_1 (and_1_out, comparator_3_eq, s2_rd_en, not_1_out);
  and and_2 (and_2_out, s2_rd_en, comparator_4_eq, not_2_out);
  regfile32x32 regfile32x32_1 (
    .rd_wr_en(s2_rd_en), .rd_wr_val(s2_rd_val), .rd_wr_sel(s2_rd_sel), .rs1_sel(idecoder_1_rs1),
    .rs2_sel(idecoder_1_rs2), .clk(clk), .rst(rst), .rs1_val(regfile32x32_1_rs1_val),
    .rs2_val(regfile32x32_1_rs2_val));
  and and_3 (ready_stall, ~or_1_out, idecoder_1_ready_stall);  // AND_Gate
  Multiplexer #(.width(32)) multiplexer_4 (
    .in0(regfile32x32_1_rs1_val), .in1(s2_rd_val), .out(rs1_val), .sel(and_1_out));
  Multiplexer #(.width(32)) multiplexer_5 (
    .in0(regfile32x32_1_rs2_val), .in1(s2_rd_val), .out(rs2_val), .sel(and_2_out));

  assign pc[1:0] = 2'b00;

  // Other names for the same wires on the sheet: C = clk; pc_decide[1:0] = {b_nt_err, b_taken_err}; R = rst;
  //   rs1_jalr[31:0] = rs1_val

  // Notes on the sheet:
  //   pc
  //   stall s2 in next cycle
endmodule

module s1_s2_pipe (
  input  [31:0] s1_pc,
  input  [31:0] s1_rs1_val,
  input  [31:0] s1_rs2_val,
  input  [18:0] s1_inst_meta_data,
  input  [31:0] s1_imm_val,
  input  s1_ready_stall,
  input  [31:0] s1_br_imm,
  input  clk,
  input  rst,
  output [31:0] s2_pc,
  output [31:0] s2_rs1_val,
  output [31:0] s2_rs2_val,
  output [18:0] s2_inst_meta_data,
  output [31:0] s2_imm_val,
  output s2_ready_stall,
  output [31:0] s2_br_imm
);

  Register #(.width(32)) register_1 (.D(s1_pc), .en(s1_ready_stall), .clk(clk), .Q(s2_pc), .clr(rst));
  Register #(.width(32)) register_2 (.D(s1_rs1_val), .en(s1_ready_stall), .clk(clk), .Q(s2_rs1_val), .clr(rst));
  Register #(.width(32)) register_3 (.D(s1_rs2_val), .en(s1_ready_stall), .clk(clk), .Q(s2_rs2_val), .clr(rst));
  Register #(.width(19)) register_4 (
    .D(s1_inst_meta_data), .en(s1_ready_stall), .clk(clk), .Q(s2_inst_meta_data), .clr(rst));
  Register #(.width(32)) register_5 (.D(s1_imm_val), .en(s1_ready_stall), .clk(clk), .Q(s2_imm_val), .clr(rst));
  Register #(.width(1)) register_6 (.D(s1_ready_stall), .en(1'b1), .clk(clk), .Q(s2_ready_stall), .clr(rst));
  Register #(.width(32)) register_7 (.D(s1_br_imm), .en(s1_ready_stall), .clk(clk), .Q(s2_br_imm), .clr(rst));
endmodule

module stage2 (
  input  [31:0] ld_data,
  input  [31:0] s2_pc,
  input  [31:0] s2_rs1_val,
  input  [31:0] s2_rs2_val,
  input  [18:0] s2_inst_meta_data,
  input  [31:0] s2_imm_val,
  input  s2_ready_stall,
  output [4:0] s2_rd_sel,
  output rd_en,
  output [31:0] rd_val,
  output branch,
  output [31:0] addr,
  output mem_wr_en,
  output [2:0] strobe,
  output [31:0] st_data,
  output s2_br,
  output s2_load
);

  wire control_unit_ew_stage2_1_data_wb_or_load, control_unit_ew_stage2_1_funct3_sel,
       control_unit_ew_stage2_1_funct_7, control_unit_ew_stage2_1_opcode_a_sel_pc_or_reg,
       control_unit_ew_stage2_1_opcode_b_sel_reg_or_imm, control_unit_ew_stage2_1_r_type;

  control_unit_ew_stage2 control_unit_ew_stage2_1 (
    .funct3(s2_inst_meta_data[11:9]), .inst_type_decode(s2_inst_meta_data[3:0]), .nop_stall(s2_ready_stall),
    .func_7(s2_inst_meta_data[18:12]), .funct_7(control_unit_ew_stage2_1_funct_7),
    .opcode_a_sel_pc_or_reg(control_unit_ew_stage2_1_opcode_a_sel_pc_or_reg),
    .opcode_b_sel_reg_or_imm(control_unit_ew_stage2_1_opcode_b_sel_reg_or_imm), .mem_wr_en_cntrl(mem_wr_en),
    .data_wb_or_load(control_unit_ew_stage2_1_data_wb_or_load), .mem_strobe(strobe), .rd_in_commit(rd_en),
    .funct3_sel(control_unit_ew_stage2_1_funct3_sel), .s2_br_inst(s2_br), .load(s2_load),
    .r_type(control_unit_ew_stage2_1_r_type));
  alu_v3 alu_v3_1 (
    .a_input(s2_rs1_val), .pc(s2_pc), .b_input(s2_rs2_val), .imm(s2_imm_val),
    .func_3(s2_inst_meta_data[11:9]), .func_7(s2_inst_meta_data[18:12]),
    .rs1_pc_sel(control_unit_ew_stage2_1_opcode_a_sel_pc_or_reg),
    .rs2_imm_sel(control_unit_ew_stage2_1_opcode_b_sel_reg_or_imm),
    .func_7_sel(control_unit_ew_stage2_1_funct_7), .func3_sel(control_unit_ew_stage2_1_funct3_sel),
    .r_type(control_unit_ew_stage2_1_r_type), .ALU_ADDR_OUT(addr), .branch_result(branch),
    .store_data(st_data));
  Multiplexer #(.width(32)) multiplexer_1 (
    .in0(addr), .in1(ld_data), .out(rd_val), .sel(control_unit_ew_stage2_1_data_wb_or_load));

  assign s2_rd_sel = s2_inst_meta_data[8:4];
endmodule

// decoder
module idecoder (
  input  [31:0] instruction,
  input  bp_out,
  output [4:0] rd,
  output [2:0] funct_3,
  output [4:0] rs1,
  output [4:0] rs2,
  output [6:0] funct_7,
  output [31:0] imm_stage_2,
  output [31:0] j_type_imm,
  output [31:0] b_type_imm,
  output [31:0] I_type_imm,
  output [3:0] ins_encoding_stage2,
  output pc_sel_mux_a,
  output [1:0] pc_sel_mux_b,
  output ready_stall
);

  wire and_1_out, or_1_out, or_2_out, or_3_out, or_4_out, rs1_sel, rs2_sel;
  wire [1:0] imm_select;
  wire [7:0] comparator_1_eq;
  wire [11:0] bit_extender_3_out;

  assign I_type_imm[31:11] = {{20{instruction[31]}}, instruction[31]};  // Bit_Extender bit_extender_1
  assign b_type_imm[31:12] = {{19{instruction[31]}}, instruction[31]};  // Bit_Extender bit_extender_2
  Comparator #(.mode("unsigned"), .width(7)) comparator_1 (
    .a(instruction[6:0]), .b(7'b0110111), .eq(comparator_1_eq[0]));  // open: gt, lt
  Comparator #(.mode("unsigned"), .width(7)) comparator_2 (
    .a(instruction[6:0]), .b(7'b0010111), .eq(comparator_1_eq[1]));  // open: gt, lt
  Comparator #(.mode("unsigned"), .width(7)) comparator_3 (
    .a(instruction[6:0]), .b(7'b1101111), .eq(comparator_1_eq[2]));  // open: gt, lt
  Comparator #(.mode("unsigned"), .width(7)) comparator_4 (
    .a(instruction[6:0]), .b(7'b1100111), .eq(pc_sel_mux_a));  // open: gt, lt
  Comparator #(.mode("unsigned"), .width(7)) comparator_5 (
    .a(instruction[6:0]), .b(7'b1100011), .eq(comparator_1_eq[4]));  // open: gt, lt
  Comparator #(.mode("unsigned"), .width(7)) comparator_6 (
    .a(instruction[6:0]), .b(7'b0000011), .eq(comparator_1_eq[5]));  // open: gt, lt
  Comparator #(.mode("unsigned"), .width(7)) comparator_7 (
    .a(instruction[6:0]), .b(7'b0100011), .eq(comparator_1_eq[6]));  // open: gt, lt
  Comparator #(.mode("unsigned"), .width(7)) comparator_8 (
    .a(instruction[6:0]), .b(7'b0010011), .eq(comparator_1_eq[7]));  // open: gt, lt
  Comparator #(.mode("unsigned"), .width(7)) comparator_9 (
    .a(instruction[6:0]), .b(7'b0110011), .eq(ins_encoding_stage2[3]));  // open: gt, lt
  assign bit_extender_3_out = {{11{1'b0}}, 1'b0};  // Bit_Extender bit_extender_3
  assign j_type_imm[31:20] = {{11{instruction[31]}}, instruction[31]};  // Bit_Extender bit_extender_4
  Multiplexer #(.width(5)) multiplexer_1 (.in0({5{1'b0}}), .in1(instruction[24:20]), .out(rs2), .sel(rs2_sel));
  Multiplexer #(.width(5)) multiplexer_2 (.in0(instruction[19:15]), .in1({5{1'b0}}), .out(rs1), .sel(rs1_sel));
  Multiplexer #(.select(2), .width(32)) multiplexer_3 (
    .in0({instruction[31:12], bit_extender_3_out}),
    .in1({I_type_imm[31:11], instruction[30:25], instruction[11:7]}),
    .in2({I_type_imm[31:11], instruction[30:20]}), .in3(32'h4), .out(imm_stage_2), .sel(imm_select));
  or or_1 (or_1_out, comparator_1_eq[4], comparator_1_eq[0], comparator_1_eq[1], comparator_1_eq[5], comparator_1_eq[6], comparator_1_eq[7], ins_encoding_stage2[3]);
  and and_1 (and_1_out, bp_out, comparator_1_eq[4]);
  priority_encoder priority_encoder_1 (
    .input0(or_1_out), .input1(comparator_1_eq[2]), .input2(pc_sel_mux_a), .input3(and_1_out),
    .out_addr(pc_sel_mux_b));
  or or_2 (or_2_out, comparator_1_eq[2], pc_sel_mux_a);
  or or_3 (or_3_out, comparator_1_eq[0], comparator_1_eq[1]);
  or or_4 (or_4_out, comparator_1_eq[5], comparator_1_eq[7]);
  priority_encoder priority_encoder_2 (
    .input0(or_3_out), .input1(comparator_1_eq[6]), .input2(or_4_out), .input3(or_2_out),
    .out_addr(imm_select));
  or or_5 (rs1_sel, comparator_1_eq[0], comparator_1_eq[1], comparator_1_eq[2]);
  or or_6 (rs2_sel, comparator_1_eq[4], comparator_1_eq[6], ins_encoding_stage2[3]);
  or or_7 (ins_encoding_stage2[2], comparator_1_eq[4], comparator_1_eq[5], comparator_1_eq[6], comparator_1_eq[7]);
  or or_8 (ins_encoding_stage2[1], comparator_1_eq[2], pc_sel_mux_a, comparator_1_eq[6], comparator_1_eq[7]);
  or or_9 (ins_encoding_stage2[0], comparator_1_eq[1], pc_sel_mux_a, comparator_1_eq[5], comparator_1_eq[7]);
  or or_10 (ready_stall, comparator_1_eq[0], comparator_1_eq[1], comparator_1_eq[2], pc_sel_mux_a, comparator_1_eq[4], comparator_1_eq[5], comparator_1_eq[6], comparator_1_eq[7], ins_encoding_stage2[3]);

  assign b_type_imm[11:0] = {instruction[7], instruction[30:25], instruction[11:8], 1'b0};
  assign funct_3 = instruction[14:12];
  assign funct_7 = instruction[31:25];
  assign I_type_imm[10:0] = instruction[30:20];
  assign j_type_imm[19:0] = {instruction[19:12], instruction[20], instruction[30:21], 1'b0};
  assign rd = instruction[11:7];

  // Other names for the same wires on the sheet: f7[6:0] = instruction[31:25]; f7_1 = instruction[31];
  //   rd_1 = instruction[7]; rd_4[3:0] = instruction[11:8]; opcode[6:0] = instruction[6:0];
  //   rs2_4[3:0] = instruction[24:21]; rs2_t[4:0] = instruction[24:20]; f7_6[5:0] = instruction[30:25];
  //   rs2_1 = instruction[20]; f3[2:0] = instruction[14:12]; rs1_t[4:0] = instruction[19:15]

  // Notes on the sheet:
  //   0-6 (7) opcode
  //   7 (1) rd / imm
  //   8-11 (4) rd / imm
  //   12-14 (3) funct3 / imm 
  //   15 -19 (5) rs1/ imm
  //   21-24 (4) rs2 / imm
  //   31 (1) funct7 / imm
  //   20 (1) rs2 / imm
  //   25-30 (6) funct7/ imm
  //   u_type_lui
  //   u_type_auipc
  //   j_type_jal
  //   i_type_jalr
  //   b_type
  //   i_type_load
  //   s_type_store
  //   i_type
  //   r_type
  //   u_type_imm
  //   s_type_imm
  //   u_type_lui
  //   u_type_auipc
  //   j_type_jal
  //   i_type
  //   r_type
  //   i_type_jalr
  //   b_type
  //   i_type_load
  //   s_type_store
  //   when branch hit is predicted send b_imm to jump
  //   why dissable the signal for store because rs2 alu port is engage/busy for immidiate rs1 + imm_i so it should not forward any thing but seperate op_fwd signal is implemented
endmodule

module regfile32x32 (
  input  rd_wr_en,
  input  [31:0] rd_wr_val,
  input  [4:0] rd_wr_sel,
  input  [4:0] rs1_sel,
  input  [4:0] rs2_sel,
  input  clk,
  input  rst,
  output [31:0] rs1_val,
  output [31:0] rs2_val
);

  wire decoder_1_out0, decoder_1_out1, decoder_1_out2, decoder_1_out3, decoder_1_out4, decoder_1_out5,
       decoder_1_out6, decoder_1_out7, decoder_1_out8, decoder_1_out9, decoder_1_out10, decoder_1_out11,
       decoder_1_out12, decoder_1_out13, decoder_1_out14, decoder_1_out15, decoder_1_out16, decoder_1_out17,
       decoder_1_out18, decoder_1_out19, decoder_1_out20, decoder_1_out21, decoder_1_out22, decoder_1_out23,
       decoder_1_out24, decoder_1_out25, decoder_1_out26, decoder_1_out27, decoder_1_out28, decoder_1_out29,
       decoder_1_out30, decoder_1_out31;
  wire [31:0] register_1_q, register_2_q, register_3_q, register_4_q, register_5_q, register_6_q,
       register_7_q, register_8_q, register_9_q, register_10_q, register_11_q, register_12_q, register_13_q,
       register_14_q, register_15_q, register_16_q, register_17_q, register_18_q, register_19_q,
       register_20_q, register_21_q, register_22_q, register_23_q, register_24_q, register_25_q,
       register_26_q, register_27_q, register_28_q, register_29_q, register_30_q, register_31_q;

  Decoder #(.select(5)) decoder_1 (
    .out0(decoder_1_out0), .out1(decoder_1_out1), .out2(decoder_1_out2), .out3(decoder_1_out3),
    .out4(decoder_1_out4), .out5(decoder_1_out5), .out6(decoder_1_out6), .out7(decoder_1_out7),
    .out8(decoder_1_out8), .out9(decoder_1_out9), .out10(decoder_1_out10), .out11(decoder_1_out11),
    .out12(decoder_1_out12), .out13(decoder_1_out13), .out14(decoder_1_out14), .out15(decoder_1_out15),
    .out16(decoder_1_out16), .out17(decoder_1_out17), .out18(decoder_1_out18), .out19(decoder_1_out19),
    .out20(decoder_1_out20), .out21(decoder_1_out21), .out22(decoder_1_out22), .out23(decoder_1_out23),
    .out24(decoder_1_out24), .out25(decoder_1_out25), .out26(decoder_1_out26), .out27(decoder_1_out27),
    .out28(decoder_1_out28), .out29(decoder_1_out29), .out30(decoder_1_out30), .out31(decoder_1_out31),
    .sel(rd_wr_sel), .en(rd_wr_en));
  Register #(.width(32)) register_1 (.D(rd_wr_val), .en(decoder_1_out8), .clk(clk), .Q(register_1_q), .clr(rst));
  Register #(.width(32)) register_2 (.D(rd_wr_val), .en(decoder_1_out16), .clk(clk), .Q(register_2_q), .clr(rst));
  Register #(.width(32)) register_3 (.D(rd_wr_val), .en(decoder_1_out24), .clk(clk), .Q(register_3_q), .clr(rst));
  Register #(.width(32)) register_4 (.D(rd_wr_val), .en(decoder_1_out1), .clk(clk), .Q(register_4_q), .clr(rst));
  Register #(.width(32)) register_5 (.D(rd_wr_val), .en(decoder_1_out9), .clk(clk), .Q(register_5_q), .clr(rst));
  Register #(.width(32)) register_6 (.D(rd_wr_val), .en(decoder_1_out17), .clk(clk), .Q(register_6_q), .clr(rst));
  Register #(.width(32)) register_7 (.D(rd_wr_val), .en(decoder_1_out25), .clk(clk), .Q(register_7_q), .clr(rst));
  Register #(.width(32)) register_8 (.D(rd_wr_val), .en(decoder_1_out2), .clk(clk), .Q(register_8_q), .clr(rst));
  Register #(.width(32)) register_9 (.D(rd_wr_val), .en(decoder_1_out10), .clk(clk), .Q(register_9_q), .clr(rst));
  Register #(.width(32)) register_10 (.D(rd_wr_val), .en(decoder_1_out18), .clk(clk), .Q(register_10_q), .clr(rst));
  Register #(.width(32)) register_11 (.D(rd_wr_val), .en(decoder_1_out26), .clk(clk), .Q(register_11_q), .clr(rst));
  Register #(.width(32)) register_12 (.D(rd_wr_val), .en(decoder_1_out3), .clk(clk), .Q(register_12_q), .clr(rst));
  Register #(.width(32)) register_13 (.D(rd_wr_val), .en(decoder_1_out11), .clk(clk), .Q(register_13_q), .clr(rst));
  Register #(.width(32)) register_14 (.D(rd_wr_val), .en(decoder_1_out19), .clk(clk), .Q(register_14_q), .clr(rst));
  Register #(.width(32)) register_15 (.D(rd_wr_val), .en(decoder_1_out27), .clk(clk), .Q(register_15_q), .clr(rst));
  Register #(.width(32)) register_16 (.D(rd_wr_val), .en(decoder_1_out4), .clk(clk), .Q(register_16_q), .clr(rst));
  Register #(.width(32)) register_17 (.D(rd_wr_val), .en(decoder_1_out12), .clk(clk), .Q(register_17_q), .clr(rst));
  Register #(.width(32)) register_18 (.D(rd_wr_val), .en(decoder_1_out20), .clk(clk), .Q(register_18_q), .clr(rst));
  Register #(.width(32)) register_19 (.D(rd_wr_val), .en(decoder_1_out28), .clk(clk), .Q(register_19_q), .clr(rst));
  Register #(.width(32)) register_20 (.D(rd_wr_val), .en(decoder_1_out5), .clk(clk), .Q(register_20_q), .clr(rst));
  Register #(.width(32)) register_21 (.D(rd_wr_val), .en(decoder_1_out13), .clk(clk), .Q(register_21_q), .clr(rst));
  Register #(.width(32)) register_22 (.D(rd_wr_val), .en(decoder_1_out21), .clk(clk), .Q(register_22_q), .clr(rst));
  Register #(.width(32)) register_23 (.D(rd_wr_val), .en(decoder_1_out29), .clk(clk), .Q(register_23_q), .clr(rst));
  Register #(.width(32)) register_24 (.D(rd_wr_val), .en(decoder_1_out6), .clk(clk), .Q(register_24_q), .clr(rst));
  Register #(.width(32)) register_25 (.D(rd_wr_val), .en(decoder_1_out14), .clk(clk), .Q(register_25_q), .clr(rst));
  Register #(.width(32)) register_26 (.D(rd_wr_val), .en(decoder_1_out22), .clk(clk), .Q(register_26_q), .clr(rst));
  Register #(.width(32)) register_27 (.D(rd_wr_val), .en(decoder_1_out30), .clk(clk), .Q(register_27_q), .clr(rst));
  Register #(.width(32)) register_28 (.D(rd_wr_val), .en(decoder_1_out7), .clk(clk), .Q(register_28_q), .clr(rst));
  Register #(.width(32)) register_29 (.D(rd_wr_val), .en(decoder_1_out15), .clk(clk), .Q(register_29_q), .clr(rst));
  Register #(.width(32)) register_30 (.D(rd_wr_val), .en(decoder_1_out23), .clk(clk), .Q(register_30_q), .clr(rst));
  Register #(.width(32)) register_31 (.D(rd_wr_val), .en(decoder_1_out31), .clk(clk), .Q(register_31_q), .clr(rst));
  Multiplexer #(.select(5), .width(32)) multiplexer_1 (
    .in0({32{1'b0}}), .in1(register_4_q), .in2(register_8_q), .in3(register_12_q), .in4(register_16_q),
    .in5(register_20_q), .in6(register_24_q), .in7(register_28_q), .in8(register_1_q), .in9(register_5_q),
    .in10(register_9_q), .in11(register_13_q), .in12(register_17_q), .in13(register_21_q),
    .in14(register_25_q), .in15(register_29_q), .in16(register_2_q), .in17(register_6_q),
    .in18(register_10_q), .in19(register_14_q), .in20(register_18_q), .in21(register_22_q),
    .in22(register_26_q), .in23(register_30_q), .in24(register_3_q), .in25(register_7_q),
    .in26(register_11_q), .in27(register_15_q), .in28(register_19_q), .in29(register_23_q),
    .in30(register_27_q), .in31(register_31_q), .out(rs1_val), .sel(rs1_sel));
  Multiplexer #(.select(5), .width(32)) multiplexer_2 (
    .in0({32{1'b0}}), .in1(register_4_q), .in2(register_8_q), .in3(register_12_q), .in4(register_16_q),
    .in5(register_20_q), .in6(register_24_q), .in7(register_28_q), .in8(register_1_q), .in9(register_5_q),
    .in10(register_9_q), .in11(register_13_q), .in12(register_17_q), .in13(register_21_q),
    .in14(register_25_q), .in15(register_29_q), .in16(register_2_q), .in17(register_6_q),
    .in18(register_10_q), .in19(register_14_q), .in20(register_18_q), .in21(register_22_q),
    .in22(register_26_q), .in23(register_30_q), .in24(register_3_q), .in25(register_7_q),
    .in26(register_11_q), .in27(register_15_q), .in28(register_19_q), .in29(register_23_q),
    .in30(register_27_q), .in31(register_31_q), .out(rs2_val), .sel(rs2_sel));
endmodule

module alu_v3 (
  input  [31:0] a_input,
  input  [31:0] pc,
  input  [31:0] b_input,
  input  [31:0] imm,
  input  [2:0] func_3,
  input  [6:0] func_7,
  input  rs1_pc_sel,
  input  rs2_imm_sel,
  input  func_7_sel,
  input  func3_sel,
  input  r_type,
  output [31:0] ALU_ADDR_OUT,
  output branch_result,
  output [31:0] store_data
);

  wire and_2_out, comparator_1_eq, not_2_out, not_3_out, not_4_out;
  wire [0:0] comparator_1_lt, comparator_2_lt;
  wire [2:0] multiplexer_8_out;
  wire [4:0] multiplexer_2_out;
  wire [6:0] multiplexer_3_out;
  wire [26:0] multiplexer_2_out_2;
  wire [31:0] adder_1_out, and_1_out, multiplexer_1_out, multiplexer_4_out, multiplexer_5_out,
       multiplexer_6_out, multiplexer_7_out, multiplier_1_cout, multiplier_1_out, multiplier_2_cout,
       not_1_out, or_1_out, shifter_1_out, shifter_2_out, shifter_3_out, xor_1_out;
  wire [63:0] bit_extender_1_out, bit_extender_2_out, multiplier_3_out;

  Multiplexer #(.width(32)) multiplexer_1 (.in0(a_input), .in1(pc), .out(multiplexer_1_out), .sel(rs1_pc_sel));
  Multiplexer #(.width(32)) multiplexer_2 (
    .in0(b_input), .in1(imm), .out({multiplexer_2_out_2, multiplexer_2_out}), .sel(rs2_imm_sel));
  Multiplexer #(.width(7)) multiplexer_3 (.in0({7{1'b0}}), .in1(func_7), .out(multiplexer_3_out), .sel(func_7_sel));
  // Probe on multiplexer_1_out
  // Probe on multiplexer_1_out
  // Probe on multiplexer_1_out
  Multiplexer #(.width(32)) multiplexer_4 (
    .in0({multiplexer_2_out_2, multiplexer_2_out}), .in1(not_1_out), .out(multiplexer_4_out),
    .sel(multiplexer_3_out[5]));
  assign not_1_out = ~{multiplexer_2_out_2, multiplexer_2_out};  // NOT_Gate not_1, 32 bits wide
  Multiplier #(.mode("twosComplement"), .width(32)) multiplier_1 (
    .a(multiplexer_1_out), .b({multiplexer_2_out_2, multiplexer_2_out}), .out(multiplier_1_out),
    .cout(multiplier_1_cout));  // open: cin
  Multiplier #(.width(32)) multiplier_2 (
    .a(multiplexer_1_out), .b({multiplexer_2_out_2, multiplexer_2_out}), .cout(multiplier_2_cout));  // open: out, cin
  assign bit_extender_1_out = {{32{multiplexer_1_out[31]}}, multiplexer_1_out};  // Bit_Extender bit_extender_1
  assign bit_extender_2_out = {{32{1'b0}}, {multiplexer_2_out_2, multiplexer_2_out}};  // Bit_Extender bit_extender_2
  Adder #(.width(32)) adder_1 (
    .a(multiplexer_1_out), .b(multiplexer_4_out), .out(adder_1_out), .cin(multiplexer_3_out[5]));  // open: cout
  Shifter #(.width(32)) shifter_1 (.in(multiplexer_1_out), .\dist (multiplexer_2_out), .out(shifter_1_out));
  Comparator #(.width(32)) comparator_1 (
    .a(multiplexer_1_out), .b({multiplexer_2_out_2, multiplexer_2_out}), .eq(comparator_1_eq),
    .lt(comparator_1_lt[0]));  // open: gt
  Comparator #(.mode("unsigned"), .width(32)) comparator_2 (
    .a(multiplexer_1_out), .b({multiplexer_2_out_2, multiplexer_2_out}), .lt(comparator_2_lt[0]));  // open: gt, eq
  assign xor_1_out = {multiplexer_2_out_2, multiplexer_2_out} ^ multiplexer_1_out;  // XOR_Gate xor_1, 32 bits wide
  Shifter #(.shift("lr"), .width(32)) shifter_2 (
    .in(multiplexer_1_out), .\dist (multiplexer_2_out), .out(shifter_2_out));
  Shifter #(.shift("ar"), .width(32)) shifter_3 (
    .in(multiplexer_1_out), .\dist (multiplexer_2_out), .out(shifter_3_out));
  assign or_1_out = multiplexer_1_out | {multiplexer_2_out_2, multiplexer_2_out};  // OR_Gate or_1, 32 bits wide
  assign and_1_out = multiplexer_1_out & {multiplexer_2_out_2, multiplexer_2_out};  // AND_Gate and_1, 32 bits wide
  Multiplier #(.width(64)) multiplier_3 (
    .a(bit_extender_1_out), .b(bit_extender_2_out), .out(multiplier_3_out));  // open: cin, cout
  // Probe on {multiplexer_2_out_2, multiplexer_2_out}
  // Probe on {multiplexer_2_out_2, multiplexer_2_out}
  // Probe on {multiplexer_2_out_2, multiplexer_2_out}
  Multiplexer #(.width(32)) multiplexer_5 (
    .in0(shifter_2_out), .in1(shifter_3_out), .out(multiplexer_5_out), .sel(multiplexer_3_out[5]));
  Multiplexer #(.select(2), .width(32)) multiplexer_6 (
    .in0(multiplier_1_out), .in1(multiplier_1_cout), .in2(multiplier_3_out[63:32]), .in3(multiplier_2_cout),
    .out(multiplexer_6_out), .sel(func_3[1:0]));
  // Probe on adder_1_out
  // Probe on adder_1_out
  // Probe on adder_1_out
  Multiplexer #(.select(3), .width(32)) multiplexer_7 (
    .in0(adder_1_out), .in1(shifter_1_out), .in2({{31{1'b0}}, comparator_1_lt[0]}),
    .in3({{31{1'b0}}, comparator_2_lt[0]}), .in4(xor_1_out), .in5(multiplexer_5_out), .in6(or_1_out),
    .in7(and_1_out), .out(multiplexer_7_out), .sel(multiplexer_8_out));
  Multiplexer #(.width(3)) multiplexer_8 (.in0(func_3), .in1(3'b000), .out(multiplexer_8_out), .sel(func3_sel));
  not not_2 (not_2_out, comparator_1_eq);
  Multiplexer #(.select(3)) multiplexer_9 (
    .in0(comparator_1_eq), .in1(not_2_out), .in2(1'b0), .in3(1'b0), .in4(comparator_1_lt[0]),
    .in5(not_3_out), .in6(comparator_2_lt[0]), .in7(not_4_out), .out(branch_result), .sel(multiplexer_8_out));
  not not_3 (not_3_out, comparator_1_lt[0]);
  not not_4 (not_4_out, comparator_2_lt[0]);
  Multiplexer #(.width(32)) multiplexer_10 (
    .in0(multiplexer_7_out), .in1(multiplexer_6_out), .out(ALU_ADDR_OUT), .sel(and_2_out));
  and and_2 (and_2_out, ~func_7[6], ~func_7[5], ~func_7[4], ~func_7[3], ~func_7[2], ~func_7[1], func_7[0], r_type);  // AND_Gate

  assign store_data = b_input;

  // Other names for the same wires on the sheet: f_3[2:0] = func_3; f_7[6:0] = func_7

  // Notes on the sheet:
  //   0). 000 --> ADD/SUB
  //   4). 100 --> XOR
  //   5). 101 --> SRL/SRA
  //   6). 110 --> OR
  //   7). 111 --> AND
  //   1). 001 --> SLL
  //   2). 010 --> SLT
  //   3). 011 --> SLTU, unsigned ADD/SUB
endmodule

module control_unit_ew_stage2 (
  input  [2:0] funct3,
  input  [3:0] inst_type_decode,
  input  nop_stall,
  input  [6:0] func_7,
  output funct_7,
  output opcode_a_sel_pc_or_reg,
  output opcode_b_sel_reg_or_imm,
  output mem_wr_en_cntrl,
  output data_wb_or_load,
  output [2:0] mem_strobe,
  output rd_in_commit,
  output funct3_sel,
  output s2_br_inst,
  output load,
  output r_type
);

  wire and_1_out, and_2_out, and_3_out, and_4_out, and_5_out, nor_1_out, not_1_out, or_5_out;
  wire [7:0] decoder_1_out0;

  Decoder #(.select(3)) decoder_1 (
    .out0(decoder_1_out0[0]), .out1(decoder_1_out0[1]), .out2(decoder_1_out0[2]), .out3(decoder_1_out0[3]),
    .out4(s2_br_inst), .out5(data_wb_or_load), .out6(mem_wr_en_cntrl), .out7(decoder_1_out0[7]),
    .sel(inst_type_decode[2:0]), .en(and_1_out));
  and and_1 (and_1_out, nop_stall, not_1_out);
  not not_1 (not_1_out, inst_type_decode[3]);
  or or_1 (opcode_a_sel_pc_or_reg, decoder_1_out0[1], decoder_1_out0[2], decoder_1_out0[3]);
  or or_2 (rd_in_commit, decoder_1_out0[0], decoder_1_out0[1], decoder_1_out0[2], decoder_1_out0[3], data_wb_or_load, decoder_1_out0[7], inst_type_decode[3]);
  or or_3 (funct3_sel, data_wb_or_load, decoder_1_out0[0], decoder_1_out0[1], decoder_1_out0[2], mem_wr_en_cntrl);
  or or_4 (opcode_b_sel_reg_or_imm, decoder_1_out0[0], decoder_1_out0[1], decoder_1_out0[2], mem_wr_en_cntrl, decoder_1_out0[3], data_wb_or_load, decoder_1_out0[7]);
  or or_5 (or_5_out, inst_type_decode[3], decoder_1_out0[7]);
  and and_2 (and_2_out, inst_type_decode[3], func_7[0]);
  and and_3 (and_3_out, funct3[2], ~funct3[1], funct3[0]);  // AND_Gate
  and and_4 (and_4_out, or_5_out, and_3_out);
  and and_5 (and_5_out, inst_type_decode[3], nor_1_out);
  or or_6 (funct_7, and_4_out, and_2_out, and_5_out);
  nor nor_1 (nor_1_out, funct3[2], funct3[1], funct3[0]);

  assign load = data_wb_or_load;
  assign mem_strobe = funct3;
  assign r_type = inst_type_decode[3];

  // Notes on the sheet:
  //   u_type_lui
  //   u_type_auipc
  //   j_type_jal
  //   b_type
  //   i_type_load
  //   i_type
  //   r_type
  //   i_type_jalr
  //   s_type_store
  //   make func_7 available when there its a mul instruction
endmodule

module priority_encoder (
  input  input0,
  input  input1,
  input  input2,
  input  input3,
  output [1:0] out_addr
);

  wire and_1_out, not_1_out;

  not not_1 (not_1_out, input2);
  or or_1 (out_addr[1], input3, input2);
  and and_1 (and_1_out, not_1_out, input1);
  or or_2 (out_addr[0], input3, and_1_out);
endmodule

module memory (
  input  [31:0] data_in,
  input  [13:0] addr,
  input  slave_en,
  input  wr_en,
  input  [2:0] strobe,
  input  clk,
  output [31:0] data_out
);

  wire and_1_out, and_2_out, and_3_out, and_4_out, and_5_out, not_1_out;
  wire [1:1] decoder_2_out0, decoder_2_out1;
  wire [3:0] decoder_1_out0, multiplexer_1_out;
  wire [7:0] multiplexer_3_out;
  wire [15:0] bank0_dout, bank2_dout, multiplexer_2_out;
  wire [31:0] shifter_1_out, zero_sign_extend_8_1_outp, zero_sign_extend_16_1_outp;

  Shifter #(.width(32)) shifter_1 (.in(data_in), .\dist ({addr[1:0], 3'b000}), .out(shifter_1_out));
  and and_1 (and_1_out, slave_en, wr_en);
  RAM #(.addrWidth(12), .asyncread("true")) bank3 (
    .addr(addr[13:2]), .we(and_2_out), .oe(1'b1), .clk(clk), .din(shifter_1_out[31:24]),
    .dout(bank2_dout[15:8]));
  Decoder #(.enable("false"), .select(2)) decoder_1 (
    .out0(decoder_1_out0[0]), .out1(decoder_1_out0[1]), .out2(decoder_1_out0[2]), .out3(decoder_1_out0[3]),
    .sel(addr[1:0]));
  Decoder #(.enable("false")) decoder_2 (.out0(decoder_2_out0[1]), .out1(decoder_2_out1[1]), .sel(addr[1]));
  and and_2 (and_2_out, and_1_out, multiplexer_1_out[3]);
  Multiplexer #(.select(2), .width(4)) multiplexer_1 (
    .in0(decoder_1_out0), .in1({{2{decoder_2_out1[1]}}, {2{decoder_2_out0[1]}}}), .in2(4'b1111),
    .in3(4'b0000), .out(multiplexer_1_out), .sel(strobe[1:0]));
  RAM #(.addrWidth(12), .asyncread("true")) bank2 (
    .addr(addr[13:2]), .we(and_3_out), .oe(1'b1), .clk(clk), .din(shifter_1_out[23:16]),
    .dout(bank2_dout[7:0]));
  not not_1 (not_1_out, strobe[2]);
  and and_3 (and_3_out, and_1_out, multiplexer_1_out[2]);
  Multiplexer #(.width(16)) multiplexer_2 (.in0(bank0_dout), .in1(bank2_dout), .out(multiplexer_2_out), .sel(addr[1]));
  Multiplexer #(.select(2), .width(8)) multiplexer_3 (
    .in0(bank0_dout[7:0]), .in1(bank0_dout[15:8]), .in2(bank2_dout[7:0]), .in3(bank2_dout[15:8]),
    .out(multiplexer_3_out), .sel(addr[1:0]));
  RAM #(.addrWidth(12), .asyncread("true")) bank1 (
    .addr(addr[13:2]), .we(and_4_out), .oe(1'b1), .clk(clk), .din(shifter_1_out[15:8]),
    .dout(bank0_dout[15:8]));
  and and_4 (and_4_out, and_1_out, multiplexer_1_out[1]);
  zero_sign_extend_16 zero_sign_extend_16_1 (
    .inpt(multiplexer_2_out), .sign_ext_en(not_1_out), .outp(zero_sign_extend_16_1_outp));
  zero_sign_extend_8 zero_sign_extend_8_1 (
    .inpt(multiplexer_3_out), .sign_ext_en(not_1_out), .outp(zero_sign_extend_8_1_outp));
  Multiplexer #(.select(2), .width(32)) multiplexer_4 (
    .in0(zero_sign_extend_8_1_outp), .in1(zero_sign_extend_16_1_outp), .in2({bank2_dout, bank0_dout}),
    .in3({32{1'b0}}), .out(data_out), .sel(strobe[1:0]));
  // Probe on data_out
  RAM #(.addrWidth(12), .asyncread("true")) bank0 (
    .addr(addr[13:2]), .we(and_5_out), .oe(1'b1), .clk(clk), .din(shifter_1_out[7:0]), .dout(bank0_dout[7:0]));
  and and_5 (and_5_out, and_1_out, multiplexer_1_out[0]);
endmodule

module zero_sign_extend_8 (
  input  [7:0] inpt,
  input  sign_ext_en,
  output [31:0] outp
);

  and and_1 (outp[31], inpt[7], sign_ext_en);

  assign outp[30:0] = {{23{outp[31]}}, inpt};
endmodule

module zero_sign_extend_16 (
  input  [15:0] inpt,
  input  sign_ext_en,
  output [31:0] outp
);

  and and_1 (outp[31], inpt[15], sign_ext_en);

  assign outp[30:0] = {{15{outp[31]}}, inpt};
endmodule

module bp_8 (
  input  en,
  input  inc,
  input  [2:0] sel,
  input  clk,
  input  rst,
  input  [2:0] write_sel,
  input  [2:0] sel_1,
  output [1:0] out0,
  output [1:0] out_1
);

  wire demultiplexer_1_out0, demultiplexer_1_out1, demultiplexer_1_out2, demultiplexer_1_out3,
       demultiplexer_1_out4, demultiplexer_1_out5, demultiplexer_1_out6, demultiplexer_1_out7;
  wire [1:0] counter_2_1_out_put, counter_2_2_out_put, counter_2_3_out_put, counter_2_4_out_put,
       counter_2_5_out_put, counter_2_6_out_put, counter_2_7_out_put, counter_2_8_out_put;

  Demultiplexer #(.select(3)) demultiplexer_1 (
    .out0(demultiplexer_1_out0), .out1(demultiplexer_1_out1), .out2(demultiplexer_1_out2),
    .out3(demultiplexer_1_out3), .out4(demultiplexer_1_out4), .out5(demultiplexer_1_out5),
    .out6(demultiplexer_1_out6), .out7(demultiplexer_1_out7), .in(en), .sel(write_sel));
  counter_2 counter_2_1 (.clk(clk), .rst(rst), .inc(inc), .en(demultiplexer_1_out0), .out_put(counter_2_1_out_put));
  counter_2 counter_2_2 (.clk(clk), .rst(rst), .inc(inc), .en(demultiplexer_1_out1), .out_put(counter_2_2_out_put));
  counter_2 counter_2_3 (.clk(clk), .rst(rst), .inc(inc), .en(demultiplexer_1_out2), .out_put(counter_2_3_out_put));
  counter_2 counter_2_4 (.clk(clk), .rst(rst), .inc(inc), .en(demultiplexer_1_out3), .out_put(counter_2_4_out_put));
  counter_2 counter_2_5 (.clk(clk), .rst(rst), .inc(inc), .en(demultiplexer_1_out4), .out_put(counter_2_5_out_put));
  counter_2 counter_2_6 (.clk(clk), .rst(rst), .inc(inc), .en(demultiplexer_1_out5), .out_put(counter_2_6_out_put));
  counter_2 counter_2_7 (.clk(clk), .rst(rst), .inc(inc), .en(demultiplexer_1_out6), .out_put(counter_2_7_out_put));
  counter_2 counter_2_8 (.clk(clk), .rst(rst), .inc(inc), .en(demultiplexer_1_out7), .out_put(counter_2_8_out_put));
  Multiplexer #(.select(3), .width(2)) multiplexer_1 (
    .in0(counter_2_1_out_put), .in1(counter_2_2_out_put), .in2(counter_2_3_out_put),
    .in3(counter_2_4_out_put), .in4(counter_2_5_out_put), .in5(counter_2_6_out_put),
    .in6(counter_2_7_out_put), .in7(counter_2_8_out_put), .out(out0), .sel(sel));
  Multiplexer #(.select(3), .width(2)) multiplexer_2 (
    .in0(counter_2_1_out_put), .in1(counter_2_2_out_put), .in2(counter_2_3_out_put),
    .in3(counter_2_4_out_put), .in4(counter_2_5_out_put), .in5(counter_2_6_out_put),
    .in6(counter_2_7_out_put), .in7(counter_2_8_out_put), .out(out_1), .sel(sel_1));
endmodule

module counter_2 (
  input  clk,
  input  rst,
  input  inc,
  input  en,
  output [1:0] out_put
);

  wire a0_q, and_1_out, and_2_out, multiplexer_1_out, multiplexer_2_out, or_1_out, or_2_out;

  or or_1 (or_1_out, ~a0_q, out_put[1]);  // OR_Gate
  and and_1 (and_1_out, out_put[1], ~a0_q);  // AND_Gate
  Register #(.width(1)) a1 (.D(multiplexer_1_out), .en(en), .clk(clk), .Q(out_put[1]), .clr(rst));
  Multiplexer multiplexer_1 (.in0(and_1_out), .in1(or_1_out), .out(multiplexer_1_out), .sel(inc));
  or or_2 (or_2_out, ~out_put[1], ~a0_q);  // OR_Gate
  and and_2 (and_2_out, ~out_put[1], ~a0_q);  // AND_Gate
  Register #(.width(1)) a0 (.D(multiplexer_2_out), .en(en), .clk(clk), .Q(a0_q), .clr(rst));
  Multiplexer multiplexer_2 (.in0(or_2_out), .in1(and_2_out), .out(multiplexer_2_out), .sel(inc));
  not not_1 (out_put[0], a0_q);
  // Probe on out_put[0]
endmodule

module bp_64 (
  input  wr_en,
  input  [31:0] pc_write,
  input  inc,
  input  [31:0] pc_read0,
  input  clk,
  input  rst,
  input  [31:0] pc_read1,
  output [1:0] msb0,
  output [1:0] msb1
);

  wire demultiplexer_1_out0, demultiplexer_1_out1, demultiplexer_1_out2, demultiplexer_1_out3,
       demultiplexer_1_out4, demultiplexer_1_out5, demultiplexer_1_out6, demultiplexer_1_out7;
  wire [1:0] bp_8_1_out0, bp_8_1_out_1, bp_8_2_out0, bp_8_2_out_1, bp_8_3_out0, bp_8_3_out_1, bp_8_4_out0,
       bp_8_4_out_1, bp_8_5_out0, bp_8_5_out_1, bp_8_6_out0, bp_8_6_out_1, bp_8_7_out0, bp_8_7_out_1,
       bp_8_8_out0, bp_8_8_out_1;

  Demultiplexer #(.select(3)) demultiplexer_1 (
    .out0(demultiplexer_1_out0), .out1(demultiplexer_1_out1), .out2(demultiplexer_1_out2),
    .out3(demultiplexer_1_out3), .out4(demultiplexer_1_out4), .out5(demultiplexer_1_out5),
    .out6(demultiplexer_1_out6), .out7(demultiplexer_1_out7), .in(wr_en), .sel(pc_write[7:5]));
  bp_8 bp_8_1 (
    .en(demultiplexer_1_out0), .inc(inc), .sel(pc_read0[4:2]), .clk(clk), .rst(rst),
    .write_sel(pc_write[4:2]), .sel_1(pc_read1[4:2]), .out0(bp_8_1_out0), .out_1(bp_8_1_out_1));
  bp_8 bp_8_2 (
    .en(demultiplexer_1_out1), .inc(inc), .sel(pc_read0[4:2]), .clk(clk), .rst(rst),
    .write_sel(pc_write[4:2]), .sel_1(pc_read1[4:2]), .out0(bp_8_2_out0), .out_1(bp_8_2_out_1));
  bp_8 bp_8_3 (
    .en(demultiplexer_1_out2), .inc(inc), .sel(pc_read0[4:2]), .clk(clk), .rst(rst),
    .write_sel(pc_write[4:2]), .sel_1(pc_read1[4:2]), .out0(bp_8_3_out0), .out_1(bp_8_3_out_1));
  bp_8 bp_8_4 (
    .en(demultiplexer_1_out3), .inc(inc), .sel(pc_read0[4:2]), .clk(clk), .rst(rst),
    .write_sel(pc_write[4:2]), .sel_1(pc_read1[4:2]), .out0(bp_8_4_out0), .out_1(bp_8_4_out_1));
  bp_8 bp_8_5 (
    .en(demultiplexer_1_out4), .inc(inc), .sel(pc_read0[4:2]), .clk(clk), .rst(rst),
    .write_sel(pc_write[4:2]), .sel_1(pc_read1[4:2]), .out0(bp_8_5_out0), .out_1(bp_8_5_out_1));
  bp_8 bp_8_6 (
    .en(demultiplexer_1_out5), .inc(inc), .sel(pc_read0[4:2]), .clk(clk), .rst(rst),
    .write_sel(pc_write[4:2]), .sel_1(pc_read1[4:2]), .out0(bp_8_6_out0), .out_1(bp_8_6_out_1));
  bp_8 bp_8_7 (
    .en(demultiplexer_1_out6), .inc(inc), .sel(pc_read0[4:2]), .clk(clk), .rst(rst),
    .write_sel(pc_write[4:2]), .sel_1(pc_read1[4:2]), .out0(bp_8_7_out0), .out_1(bp_8_7_out_1));
  bp_8 bp_8_8 (
    .en(demultiplexer_1_out7), .inc(inc), .sel(pc_read0[4:2]), .clk(clk), .rst(rst),
    .write_sel(pc_write[4:2]), .sel_1(pc_read1[4:2]), .out0(bp_8_8_out0), .out_1(bp_8_8_out_1));
  Multiplexer #(.select(3), .width(2)) multiplexer_1 (
    .in0(bp_8_1_out0), .in1(bp_8_2_out0), .in2(bp_8_3_out0), .in3(bp_8_4_out0), .in4(bp_8_5_out0),
    .in5(bp_8_6_out0), .in6(bp_8_7_out0), .in7(bp_8_8_out0), .out(msb0), .sel(pc_read0[7:5]));
  Multiplexer #(.select(3), .width(2)) multiplexer_2 (
    .in0(bp_8_1_out_1), .in1(bp_8_2_out_1), .in2(bp_8_3_out_1), .in3(bp_8_4_out_1), .in4(bp_8_5_out_1),
    .in5(bp_8_6_out_1), .in6(bp_8_7_out_1), .in7(bp_8_8_out_1), .out(msb1), .sel(pc_read1[7:5]));
endmodule
